// Logisim project alu.circ as structural Verilog: 8 circuits, main circuit alu
module alu (
  input  [31:0] A,
  input  [31:0] B,
  input  [3:0] ALUSel,
  output [31:0] Result
);

  wire [31:0] add0, and1, divu8, mul10, mulhu11, or2, remu9, sll6, slt7, sra5, srl4, sub12, xor3;

  Adder #(.width(32)) adder_1 (.a(A), .b(B), .out(add0));  // open: cin, cout
  assign and1 = A & B;  // AND_Gate and_1, 32 bits wide
  assign or2 = A | B;  // OR_Gate or_1, 32 bits wide
  assign xor3 = A ^ B;  // XOR_Gate xor_1, 32 bits wide
  mySRL mysrl_1 (.A(A), .B(B), .result(srl4));
  mySRA mysra_1 (.A(A), .B(B), .Result(sra5));
  mySLL mysll_1 (.A(A), .B(B), .Result(sll6));
  Multiplier #(.width(32)) multiplier_1 (.a(A), .b(B), .out(mul10));  // open: cin, cout
  Subtractor #(.width(32)) subtractor_1 (.a(A), .b(B), .out(sub12));  // open: bin, bout
  mySLT myslt_1 (.A(A), .B(B), .Result(slt7));
  myDIVU mydivu_1 (.A(A), .B(B), .Result(divu8));
  myREMU myremu_1 (.A(A), .B(B), .Result(remu9));
  myMULHU mymulhu_1 (.A(A), .B(B), .Result(mulhu11));
  Multiplexer #(.select(4), .width(32), .enable("false")) multiplexer_1 (
    .in0(add0), .in1(and1), .in2(or2), .in3(xor3), .in4(srl4), .in5(sra5), .in6(sll6), .in7(slt7),
    .in8(divu8), .in9(remu9), .in10(mul10), .in11(mulhu11), .in12(sub12), .in13(B), .out(Result), .sel(ALUSel));  // open: in14, in15

  // Other names for the same wires on the sheet: bsel13[31:0] = B

  // Notes on the sheet:
  //   INPUTS to your circuit
  //   DON'T CHANGE THE LOCATIONS OF THE INPUTS AND OUTPUTS!
  //   OUTPUT from your circuit
endmodule

module mySRL (
  input  [31:0] A,
  input  [31:0] B,
  output [31:0] result
);

  Shifter #(.width(32), .shift("lr")) shifter_1 (.in(A), .\dist (B[4:0]), .out(result));
endmodule

module mySRA (
  input  [31:0] A,
  input  [31:0] B,
  output [31:0] Result
);

  Shifter #(.width(32), .shift("ar")) shifter_1 (.in(A), .\dist (B[4:0]), .out(Result));
endmodule

module mySLL (
  input  [31:0] A,
  input  [31:0] B,
  output [31:0] Result
);

  Shifter #(.width(32)) shifter_1 (.in(A), .\dist (B[4:0]), .out(Result));
endmodule

module mySLT (
  input  [31:0] A,
  input  [31:0] B,
  output [31:0] Result
);

  Comparator #(.width(32)) comparator_1 (.a(A), .b(B), .lt(Result[0]));  // open: gt, eq

  assign Result[31:1] = {31{1'b0}};
endmodule

module myDIVU (
  input  [31:0] A,
  input  [31:0] B,
  output [31:0] Result
);

  wire comparator_1_eq;
  wire [31:0] divider_1_out;

  Divider #(.width(32)) divider_1 (.a(A), .b(B), .out(divider_1_out));  // open: upper, rem
  Multiplexer #(.width(32), .enable("false")) multiplexer_1 (
    .in0(divider_1_out), .in1({32{1'b1}}), .out(Result), .sel(comparator_1_eq));
  Comparator #(.width(32)) comparator_1 (.a(B), .b({32{1'b0}}), .eq(comparator_1_eq));  // open: gt, lt
endmodule

module myREMU (
  input  [31:0] A,
  input  [31:0] B,
  output [31:0] Result
);

  wire comparator_1_eq;
  wire [31:0] divider_1_rem;

  Divider #(.width(32)) divider_1 (.a(A), .b(B), .rem(divider_1_rem));  // open: out, upper
  Multiplexer #(.width(32), .enable("false")) multiplexer_1 (
    .in0(divider_1_rem), .in1(A), .out(Result), .sel(comparator_1_eq));
  Comparator #(.width(32)) comparator_1 (.a(B), .b({32{1'b0}}), .eq(comparator_1_eq));  // open: gt, lt
endmodule

module myMULHU (
  input  [31:0] A,
  input  [31:0] B,
  output [31:0] Result
);

  Multiplier #(.width(32)) multiplier_1 (.a(A), .b(B), .cout(Result));  // open: out, cin
endmodule
