// Logisim project cpu.circ as structural Verilog: 11 circuits, main circuit main
module main (
  input  [31:0] INSTRUCTION,
  input  CLOCK,
  output [31:0] PROGRAM_COUNTER,
  output [31:0] ra,
  output [31:0] sp,
  output [31:0] t0,
  output [31:0] t1,
  output [31:0] t2,
  output [31:0] s0,
  output [31:0] s1,
  output [31:0] a0
);

  wire a_sel, BrEq, BrLT, bsel, comparator_1_eq, comparator_3_eq, comparator_4_eq, comparator_5_eq,
       comparator_6_eq, comparator_7_eq, comparator_8_eq, comparator_9_eq, memRW, myEnable, pc_sel,
       s23_opcode;
  wire [1:0] wb_sel;
  wire [2:0] func3;
  wire [3:0] my_alu_sel;
  wire [4:0] rd, rs1, rs2;
  wire [6:0] func7, opcode;
  wire [11:0] imm;
  wire [31:0] adder_1_out, adder_2_out, alu_result, DMEM_p5, imm_ext, multiplexer_1_out, multiplexer_2_out,
       multiplexer_3_out, multiplexer_4_out, nop_1_out_1, pipe_instr, Piped_PC, RegFile_read_data_1,
       RegFile_read_data_2, wb;

  Adder #(.width(32)) adder_1 (.a(PROGRAM_COUNTER), .b(32'h4), .out(adder_1_out));  // open: cin, cout
  nop nop_1 (.out_1(nop_1_out_1));
  Multiplexer #(.width(32), .enable("false")) multiplexer_1 (
    .in0(INSTRUCTION), .in1(nop_1_out_1), .out(multiplexer_1_out), .sel(pc_sel));
  instru_decode instru_decode_1 (
    .instruction(pipe_instr), .opcode(opcode), .rd(rd), .func3(func3), .rs1(rs1), .imm(imm), .rs2(rs2),
    .func7(func7));
  ASel asel_1 (.opcode(opcode), .func3(func3), .func7(func7), .out_4(a_sel));
  Multiplexer #(.width(32), .enable("false")) multiplexer_2 (
    .in0(adder_1_out), .in1(alu_result), .out(multiplexer_2_out), .sel(pc_sel));
  Register #(.width(32)) pipelined (.D(multiplexer_1_out), .en(1'b1), .clk(CLOCK), .Q(pipe_instr));  // open: clr
  Register #(.width(32)) u_piped_PC (.D(PROGRAM_COUNTER), .en(1'b1), .clk(CLOCK), .Q(Piped_PC));  // open: clr
  Register #(.width(32)) PC (.D(multiplexer_2_out), .clk(CLOCK), .Q(PROGRAM_COUNTER));  // open: en, clr
  ALU_Sel alu_sel_1 (.Opcode(opcode), .alu_sel(my_alu_sel), .func3(func3), .func7(func7));
  B_Sel b_sel_1 (.opcode(opcode), .func3(func3), .func7(func7), .Result(bsel));
  PCSel pcsel_1 (.Opcode(opcode), .func3(func3), .func7(func7), .BrEq(BrEq), .BrLt(BrLT), .out_6(pc_sel));
  imm_gen imm_gen_1 (.instr_input(pipe_instr), .Imm_output(imm_ext));
  regfile_main RegFile (
    .rs2(rs2), .rd(rd), .Read_Data_1(RegFile_read_data_1), .Read_Data_2(RegFile_read_data_2), .ra(ra),
    .sp(sp), .t0(t0), .t1(t1), .t2(t2), .s0(s0), .s1(s1), .a0(a0), .rs1(rs1), .Write_Data(wb),
    .RegWEn(myEnable), .clk(CLOCK));
  Comparator #(.width(3), .mode("unsigned")) comparator_1 (
    .a(func3), .b(3'b010), .eq(comparator_1_eq));  // open: gt, lt
  Comparator #(.width(7), .mode("unsigned")) comparator_2 (
    .a(opcode), .b(7'b0100011), .eq(s23_opcode));  // open: gt, lt
  WBSel wbsel_1 (.opcode(opcode), .func3(func3), .func7(func7), .out_4(wb_sel));
  and and_1 (memRW, s23_opcode, comparator_1_eq);
  Branch_Comp branch_comp_1 (
    .opcode(opcode), .func3(func3), .RegA(RegFile_read_data_1), .RegB(RegFile_read_data_2), .BrEq(BrEq),
    .BLT(BrLT));
  Multiplexer #(.width(32), .enable("false")) multiplexer_3 (
    .in0(RegFile_read_data_2), .in1(imm_ext), .out(multiplexer_3_out), .sel(bsel));
  Multiplexer #(.width(32), .enable("false")) multiplexer_4 (
    .in0(RegFile_read_data_1), .in1(Piped_PC), .out(multiplexer_4_out), .sel(a_sel));
  alu Arithmetic_Logic_Unit (.ALUSel(my_alu_sel), .B(multiplexer_3_out), .A(multiplexer_4_out), .Result(alu_result));
  Comparator #(.width(7), .mode("unsigned")) comparator_3 (
    .a(opcode), .b(7'b0000011), .eq(comparator_3_eq));  // open: gt, lt
  Comparator #(.width(7), .mode("unsigned")) comparator_4 (
    .a(opcode), .b(7'b0010011), .eq(comparator_4_eq));  // open: gt, lt
  Comparator #(.width(7), .mode("unsigned")) comparator_5 (
    .a(opcode), .b(7'b0110111), .eq(comparator_5_eq));  // open: gt, lt
  Comparator #(.width(7), .mode("unsigned")) comparator_6 (
    .a(opcode), .b(7'b0110011), .eq(comparator_6_eq));  // open: gt, lt
  Comparator #(.width(7), .mode("unsigned")) comparator_7 (
    .a(opcode), .b(7'b0011011), .eq(comparator_7_eq));  // open: gt, lt
  Comparator #(.width(7), .mode("unsigned")) comparator_8 (
    .a(opcode), .b(7'b1101111), .eq(comparator_8_eq));  // open: gt, lt
  Comparator #(.width(7), .mode("unsigned")) comparator_9 (
    .a(opcode), .b(7'b1100111), .eq(comparator_9_eq));  // open: gt, lt
  or or_1 (myEnable, comparator_3_eq, comparator_4_eq, comparator_5_eq, comparator_6_eq, comparator_7_eq, comparator_8_eq, comparator_9_eq);
  // mem_main DMEM: pin names not known; wires that end beside it: alu_result, RegFile_read_data_2, CLOCK, memRW, DMEM_p5
  Adder #(.width(32)) adder_2 (.a(Piped_PC), .b(32'h4), .out(adder_2_out));  // open: cin, cout
  Multiplexer #(.select(2), .width(32), .enable("false")) multiplexer_5 (
    .in0(DMEM_p5), .in1(alu_result), .in2(adder_2_out), .out(wb), .sel(wb_sel));  // open: in3

  // Other names for the same wires on the sheet: clk = CLOCK

  // Notes on the sheet:
  //   Output
  //   Instruction Decode
  //   IMEM (do **NOT** move this)
  //   Inputs
  //   It is OK to move the PC, RegFile, ALU, and MEM to wherever is most convenient for you when constructing your CPU, and to delete this text
  //   Inputs/Outputs for testing. Do **NOT** move these.
  //   Write to Memory if SW
  //   RegWen
endmodule

module imm_gen (
  input  [31:0] instr_input,
  output [31:0] Imm_output
);

  wire and_1_out, and_2_out, and_3_out, and_6_out, and_7_out, and_8_out, and_9_out, and_10_out, and_11_out,
       and_12_out, and_13_out, and_14_out, and_15_out, and_16_out, and_17_out, b63_opcode, b_type_sel,
       comparator_1_eq, comparator_2_eq, comparator_3_eq, comparator_4_eq, comparator_8_eq, comparator_9_eq,
       comparator_10_eq, comparator_11_eq, comparator_12_eq, comparator_17_eq, comparator_18_eq,
       comparator_19_eq, comparator_20_eq, comparator_21_eq, comparator_22_eq, comparator_23_eq,
       comparator_24_eq, comparator_25_eq, comparator_26_eq, comparator_27_eq, i3, i3_opcode, i13,
       i13_opcode, i67, i67_opcode, i_ex, i_type_sel, j_type_sel, nor_1_out, s23_opcode, s_type_sel,
       u_type_sel;
  wire [31:0] multiplexer_1_out, multiplexer_2_out, multiplexer_3_out, multiplexer_7_out;

  Comparator #(.width(3), .mode("unsigned")) comparator_1 (
    .a(instr_input[14:12]), .b(3'b000), .eq(comparator_1_eq));  // open: gt, lt
  Comparator #(.width(3), .mode("unsigned")) comparator_2 (
    .a(instr_input[14:12]), .b(3'b001), .eq(comparator_2_eq));  // open: gt, lt
  Comparator #(.width(3), .mode("unsigned")) comparator_3 (
    .a(instr_input[14:12]), .b(3'b010), .eq(comparator_3_eq));  // open: gt, lt
  Comparator #(.width(3), .mode("unsigned")) comparator_4 (
    .a(instr_input[14:12]), .b(3'b000), .eq(comparator_4_eq));  // open: gt, lt
  Comparator #(.width(7), .mode("unsigned")) comparator_5 (
    .a(instr_input[6:0]), .b(7'b0000011), .eq(i3_opcode));  // open: gt, lt
  Comparator #(.width(7), .mode("unsigned")) comparator_6 (
    .a(instr_input[6:0]), .b(7'b1100111), .eq(i67_opcode));  // open: gt, lt
  and and_1 (and_1_out, i3_opcode, comparator_1_eq);
  and and_2 (and_2_out, i3_opcode, comparator_2_eq);
  and and_3 (and_3_out, i3_opcode, comparator_3_eq);
  and and_4 (i67, i67_opcode, comparator_4_eq);
  or or_1 (i3, and_1_out, and_2_out, and_3_out);
  Comparator #(.width(7), .mode("unsigned")) comparator_7 (
    .a(instr_input[6:0]), .b(7'b0100011), .eq(s23_opcode));  // open: gt, lt
  Comparator #(.width(3), .mode("unsigned")) comparator_8 (
    .a(instr_input[14:12]), .b(3'b010), .eq(comparator_8_eq));  // open: gt, lt
  Comparator #(.width(3), .mode("unsigned")) comparator_9 (
    .a(instr_input[14:12]), .b(3'b000), .eq(comparator_9_eq));  // open: gt, lt
  Comparator #(.width(3), .mode("unsigned")) comparator_10 (
    .a(instr_input[14:12]), .b(3'b100), .eq(comparator_10_eq));  // open: gt, lt
  Comparator #(.width(3), .mode("unsigned")) comparator_11 (
    .a(instr_input[14:12]), .b(3'b110), .eq(comparator_11_eq));  // open: gt, lt
  Comparator #(.width(3), .mode("unsigned")) comparator_12 (
    .a(instr_input[14:12]), .b(3'b001), .eq(comparator_12_eq));  // open: gt, lt
  Comparator #(.width(7), .mode("unsigned")) comparator_13 (
    .a(instr_input[6:0]), .b(7'b1100011), .eq(b63_opcode));  // open: gt, lt
  Comparator #(.width(7), .mode("unsigned")) comparator_14 (
    .a(instr_input[6:0]), .b(7'b0110111), .eq(u_type_sel));  // open: gt, lt
  Comparator #(.width(7), .mode("unsigned")) comparator_15 (
    .a(instr_input[6:0]), .b(7'b1101111), .eq(j_type_sel));  // open: gt, lt
  and and_5 (s_type_sel, s23_opcode, comparator_8_eq);
  and and_6 (and_6_out, b63_opcode, comparator_9_eq);
  and and_7 (and_7_out, b63_opcode, comparator_10_eq);
  and and_8 (and_8_out, b63_opcode, comparator_11_eq);
  and and_9 (and_9_out, b63_opcode, comparator_12_eq);
  Comparator #(.width(7), .mode("unsigned")) comparator_16 (
    .a(instr_input[6:0]), .b(7'b0010011), .eq(i13_opcode));  // open: gt, lt
  Comparator #(.width(3), .mode("unsigned")) comparator_17 (
    .a(instr_input[14:12]), .b(3'b000), .eq(comparator_17_eq));  // open: gt, lt
  Comparator #(.width(3), .mode("unsigned")) comparator_18 (
    .a(instr_input[14:12]), .b(3'b010), .eq(comparator_18_eq));  // open: gt, lt
  Comparator #(.width(3), .mode("unsigned")) comparator_19 (
    .a(instr_input[14:12]), .b(3'b100), .eq(comparator_19_eq));  // open: gt, lt
  Comparator #(.width(3), .mode("unsigned")) comparator_20 (
    .a(instr_input[14:12]), .b(3'b110), .eq(comparator_20_eq));  // open: gt, lt
  Comparator #(.width(3), .mode("unsigned")) comparator_21 (
    .a(instr_input[14:12]), .b(3'b111), .eq(comparator_21_eq));  // open: gt, lt
  or or_2 (b_type_sel, and_6_out, and_7_out, and_8_out, and_9_out);
  and and_10 (and_10_out, i13_opcode, comparator_17_eq);
  and and_11 (and_11_out, i13_opcode, comparator_18_eq);
  and and_12 (and_12_out, i13_opcode, comparator_19_eq);
  and and_13 (and_13_out, i13_opcode, comparator_20_eq);
  and and_14 (and_14_out, i13_opcode, comparator_21_eq);
  or or_3 (i13, and_10_out, and_11_out, and_12_out, and_13_out, and_14_out);
  Comparator #(.width(3), .mode("unsigned")) comparator_22 (
    .a(instr_input[14:12]), .b(3'b001), .eq(comparator_22_eq));  // open: gt, lt
  Comparator #(.width(7), .mode("unsigned")) comparator_23 (
    .a(instr_input[31:25]), .b({7{1'b0}}), .eq(comparator_23_eq));  // open: gt, lt
  Comparator #(.width(3), .mode("unsigned")) comparator_24 (
    .a(instr_input[14:12]), .b(3'b101), .eq(comparator_24_eq));  // open: gt, lt
  Comparator #(.width(7), .mode("unsigned")) comparator_25 (
    .a(instr_input[31:25]), .b({7{1'b0}}), .eq(comparator_25_eq));  // open: gt, lt
  Comparator #(.width(3), .mode("unsigned")) comparator_26 (
    .a(instr_input[14:12]), .b(3'b101), .eq(comparator_26_eq));  // open: gt, lt
  Comparator #(.width(7), .mode("unsigned")) comparator_27 (
    .a(instr_input[31:25]), .b(7'b0100000), .eq(comparator_27_eq));  // open: gt, lt
  or or_4 (i_type_sel, i3, i13, i67);
  and and_15 (and_15_out, i13_opcode, comparator_22_eq, comparator_23_eq);
  and and_16 (and_16_out, i13_opcode, comparator_24_eq, comparator_25_eq);
  and and_17 (and_17_out, i13_opcode, comparator_26_eq, comparator_27_eq);
  or or_5 (i_ex, and_15_out, and_16_out, and_17_out);
  Multiplexer #(.width(32), .enable("false")) multiplexer_1 (
    .in0({{20{1'b0}}, instr_input[31:20]}), .in1({{20{1'b1}}, instr_input[31:20]}), .out(multiplexer_1_out),
    .sel(instr_input[31]));
  Multiplexer #(.width(32), .enable("false")) multiplexer_2 (
    .in0({{20{1'b0}}, instr_input[31:25], instr_input[11:7]}),
    .in1({{20{1'b1}}, instr_input[31:25], instr_input[11:7]}), .out(multiplexer_2_out), .sel(instr_input[31]));
  Multiplexer #(.width(32), .enable("false")) multiplexer_3 (
    .in0({{19{1'b0}}, instr_input[31], instr_input[7], instr_input[30:25], instr_input[11:8], 1'b0}),
    .in1({{19{1'b1}}, instr_input[31], instr_input[7], instr_input[30:25], instr_input[11:8], 1'b0}),
    .out(multiplexer_3_out), .sel(instr_input[31]));
  Multiplexer #(.width(32), .enable("false")) multiplexer_4 (
    .in1({instr_input[31:12], {12{1'b0}}}), .out(Imm_output), .sel(u_type_sel));  // open: in0
  nor nor_1 (nor_1_out, i_type_sel, s_type_sel, b_type_sel, u_type_sel, j_type_sel, i_ex);
  Multiplexer #(.width(32), .enable("false")) multiplexer_5 (
    .in1(multiplexer_1_out), .out(Imm_output), .sel(i_type_sel));  // open: in0
  Multiplexer #(.width(32), .enable("false")) multiplexer_6 (
    .in1({{27{1'b0}}, instr_input[24:20]}), .out(Imm_output), .sel(i_ex));  // open: in0
  Multiplexer #(.width(32), .enable("false")) multiplexer_7 (
    .in0({{11{1'b0}}, instr_input[31], instr_input[19:12], instr_input[20], instr_input[30:21], 1'b0}),
    .in1({{11{1'b1}}, instr_input[31], instr_input[19:12], instr_input[20], instr_input[30:21], 1'b0}),
    .out(multiplexer_7_out), .sel(instr_input[31]));
  Multiplexer #(.width(32), .enable("false")) multiplexer_8 (
    .in1({32{1'b0}}), .out(Imm_output), .sel(nor_1_out));  // open: in0
  Multiplexer #(.width(32), .enable("false")) multiplexer_9 (
    .in1(multiplexer_2_out), .out(Imm_output), .sel(s_type_sel));  // open: in0
  Multiplexer #(.width(32), .enable("false")) multiplexer_10 (
    .in1(multiplexer_3_out), .out(Imm_output), .sel(b_type_sel));  // open: in0
  Multiplexer #(.width(32), .enable("false")) multiplexer_11 (
    .in1(multiplexer_7_out), .out(Imm_output), .sel(j_type_sel));  // open: in0

  // Other names for the same wires on the sheet: b_imm_11 = instr_input[7]; rd[4:0] = instr_input[11:7];
  //   s_imm_4_0[4:0] = instr_input[11:7]; b_imm_4_1[3:0] = instr_input[11:8]; b_imm_10_5[5:0] = instr_input[30:25];
  //   func7[6:0] = instr_input[31:25]; i_imm_11_0[11:0] = instr_input[31:20]; j_imm_10_1[9:0] = instr_input[30:21];
  //   s_imm_11_5[6:0] = instr_input[31:25]; u_imm_31_12[19:0] = instr_input[31:12]; func3[2:0] = instr_input[14:12];
  //   j_imm_19_12[7:0] = instr_input[19:12]; rs1[4:0] = instr_input[19:15]; b_imm_12 = instr_input[31];
  //   inst_31 = instr_input[31]; j_imm_20 = instr_input[31]; j_imm_11 = instr_input[20];
  //   rs2[4:0] = instr_input[24:20]; opcode[6:0] = instr_input[6:0]; Result[31:0] = Imm_output

  // Notes on the sheet:
  //   I-type
  //   S-type
  //   J-type
  //   B-type
  //   U-type
  //   I-exceptions
  //   S - Sign Extend
  //   B - Sign Extend
  //   I - Sign Extend
  //   J - Sign Extend
  //   U_imm
  //   I_imm
  //   slli/slri/srai_imm
  //   S_imm
  //   B_imm
  //   J_imm
endmodule

module ALU_Sel (
  input  [6:0] Opcode,
  input  [2:0] func3,
  input  [6:0] func7,
  output [3:0] alu_sel
);

  wire add, addi, andi, b63_opcode, beq, blt, bltu, bne, comparator_1_eq, comparator_2_eq, comparator_3_eq,
       comparator_4_eq, comparator_7_eq, comparator_8_eq, comparator_9_eq, comparator_10_eq,
       comparator_11_eq, comparator_12_eq, comparator_13_eq, comparator_14_eq, comparator_15_eq,
       comparator_16_eq, comparator_17_eq, comparator_20_eq, comparator_22_eq, comparator_23_eq,
       comparator_24_eq, comparator_25_eq, comparator_28_eq, comparator_29_eq, comparator_30_eq,
       comparator_31_eq, comparator_32_eq, comparator_33_eq, comparator_34_eq, comparator_35_eq,
       comparator_36_eq, comparator_37_eq, comparator_38_eq, comparator_39_eq, comparator_40_eq,
       comparator_41_eq, comparator_42_eq, comparator_43_eq, comparator_44_eq, comparator_45_eq,
       comparator_46_eq, comparator_47_eq, comparator_49_eq, comparator_50_eq, comparator_51_eq,
       comparator_52_eq, comparator_53_eq, comparator_54_eq, divu, i3_opcode, i13_opcode, i67_opcode, jal,
       jalr, lb, lh, lui, lw, mul, mulh, mulhu, my_and, my_or, my_sll, my_srl, my_xor, nor_1_out, or_1_out,
       or_2_out, or_3_out, or_4_out, or_5_out, or_6_out, or_7_out, ori, r33_opcode, remu, s23_opcode, slli,
       slt, slti, srai, srli, sub, sw, xori;

  or or_1 (or_1_out, addi, add, lw, sw);
  or or_2 (or_2_out, my_or, ori);
  or or_3 (or_3_out, my_srl, srli);
  or or_4 (or_4_out, my_sll, slli);
  Multiplexer #(.width(4), .enable("false")) multiplexer_1 (.in1(4'b0000), .out(alu_sel), .sel(or_1_out));  // open: in0
  Multiplexer #(.width(4), .enable("false")) multiplexer_2 (.in1(4'b0010), .out(alu_sel), .sel(or_2_out));  // open: in0
  Multiplexer #(.width(4), .enable("false")) multiplexer_3 (.in1(4'b0100), .out(alu_sel), .sel(or_3_out));  // open: in0
  Multiplexer #(.width(4), .enable("false")) multiplexer_4 (.in1(4'b0110), .out(alu_sel), .sel(or_4_out));  // open: in0
  Multiplexer #(.width(4), .enable("false")) multiplexer_5 (.in1(4'b1000), .out(alu_sel), .sel(divu));  // open: in0
  Multiplexer #(.width(4), .enable("false")) multiplexer_6 (.in1(4'b1010), .out(alu_sel), .sel(mul));  // open: in0
  Comparator #(.width(3), .mode("unsigned")) comparator_1 (
    .a(func3), .b(3'b000), .eq(comparator_1_eq));  // open: gt, lt
  Comparator #(.width(3), .mode("unsigned")) comparator_2 (
    .a(func3), .b(3'b001), .eq(comparator_2_eq));  // open: gt, lt
  Comparator #(.width(3), .mode("unsigned")) comparator_3 (
    .a(func3), .b(3'b010), .eq(comparator_3_eq));  // open: gt, lt
  Comparator #(.width(3), .mode("unsigned")) comparator_4 (
    .a(func3), .b(3'b000), .eq(comparator_4_eq));  // open: gt, lt
  Comparator #(.width(7), .mode("unsigned")) comparator_5 (.a(Opcode), .b(7'b0000011), .eq(i3_opcode));  // open: gt, lt
  Comparator #(.width(7), .mode("unsigned")) comparator_6 (
    .a(Opcode), .b(7'b1100111), .eq(i67_opcode));  // open: gt, lt
  or or_5 (or_5_out, my_and, andi);
  or or_6 (or_6_out, my_xor, xori);
  or or_7 (or_7_out, slt, slti);
  and and_1 (lh, i3_opcode, comparator_2_eq);
  and and_2 (lw, i3_opcode, comparator_3_eq);
  and and_3 (jalr, i67_opcode, comparator_4_eq);
  Multiplexer #(.width(4), .enable("false")) multiplexer_7 (.in1(4'b0001), .out(alu_sel), .sel(or_5_out));  // open: in0
  Multiplexer #(.width(4), .enable("false")) multiplexer_8 (.in1(4'b0011), .out(alu_sel), .sel(or_6_out));  // open: in0
  Multiplexer #(.width(4), .enable("false")) multiplexer_9 (.in1(4'b0101), .out(alu_sel), .sel(srai));  // open: in0
  Multiplexer #(.width(4), .enable("false")) multiplexer_10 (
    .in1(4'b0111), .out(alu_sel), .sel(or_7_out));  // open: in0
  Multiplexer #(.width(4), .enable("false")) multiplexer_11 (.in1(4'b1001), .out(alu_sel), .sel(remu));  // open: in0
  Multiplexer #(.width(4), .enable("false")) multiplexer_12 (.in1(4'b1100), .out(alu_sel), .sel(sub));  // open: in0
  and and_4 (lb, i3_opcode, comparator_1_eq);
  Multiplexer #(.width(4), .enable("false")) multiplexer_13 (.in1(4'b1101), .out(alu_sel), .sel(lui));  // open: in0
  Comparator #(.width(3), .mode("unsigned")) comparator_7 (
    .a(func3), .b(3'b000), .eq(comparator_7_eq));  // open: gt, lt
  Comparator #(.width(3), .mode("unsigned")) comparator_8 (
    .a(func3), .b(3'b010), .eq(comparator_8_eq));  // open: gt, lt
  Comparator #(.width(3), .mode("unsigned")) comparator_9 (
    .a(func3), .b(3'b100), .eq(comparator_9_eq));  // open: gt, lt
  Comparator #(.width(3), .mode("unsigned")) comparator_10 (
    .a(func3), .b(3'b110), .eq(comparator_10_eq));  // open: gt, lt
  Comparator #(.width(3), .mode("unsigned")) comparator_11 (
    .a(func3), .b(3'b111), .eq(comparator_11_eq));  // open: gt, lt
  Comparator #(.width(3), .mode("unsigned")) comparator_12 (
    .a(func3), .b(3'b001), .eq(comparator_12_eq));  // open: gt, lt
  Comparator #(.width(7), .mode("unsigned")) comparator_13 (
    .a(func7), .b({7{1'b0}}), .eq(comparator_13_eq));  // open: gt, lt
  Comparator #(.width(3), .mode("unsigned")) comparator_14 (
    .a(func3), .b(3'b101), .eq(comparator_14_eq));  // open: gt, lt
  Comparator #(.width(7), .mode("unsigned")) comparator_15 (
    .a(func7), .b({7{1'b0}}), .eq(comparator_15_eq));  // open: gt, lt
  Comparator #(.width(3), .mode("unsigned")) comparator_16 (
    .a(func3), .b(3'b101), .eq(comparator_16_eq));  // open: gt, lt
  Comparator #(.width(7), .mode("unsigned")) comparator_17 (
    .a(func7), .b(7'b0100000), .eq(comparator_17_eq));  // open: gt, lt
  Multiplexer #(.width(4), .enable("false")) multiplexer_14 (.in1(4'b1110), .out(alu_sel), .sel(mulh));  // open: in0
  Comparator #(.width(7), .mode("unsigned")) comparator_18 (
    .a(Opcode), .b(7'b0010011), .eq(i13_opcode));  // open: gt, lt
  and and_5 (addi, i13_opcode, comparator_7_eq);
  and and_6 (slti, i13_opcode, comparator_8_eq);
  and and_7 (xori, i13_opcode, comparator_9_eq);
  and and_8 (ori, i13_opcode, comparator_10_eq);
  and and_9 (andi, i13_opcode, comparator_11_eq);
  and and_10 (slli, i13_opcode, comparator_12_eq, comparator_13_eq);
  and and_11 (srli, i13_opcode, comparator_14_eq, comparator_15_eq);
  and and_12 (srai, i13_opcode, comparator_16_eq, comparator_17_eq);
  Comparator #(.width(7), .mode("unsigned")) comparator_19 (
    .a(Opcode), .b(7'b0100011), .eq(s23_opcode));  // open: gt, lt
  Comparator #(.width(3), .mode("unsigned")) comparator_20 (
    .a(func3), .b(3'b010), .eq(comparator_20_eq));  // open: gt, lt
  Comparator #(.width(7), .mode("unsigned")) comparator_21 (
    .a(Opcode), .b(7'b1100011), .eq(b63_opcode));  // open: gt, lt
  Comparator #(.width(3), .mode("unsigned")) comparator_22 (
    .a(func3), .b(3'b000), .eq(comparator_22_eq));  // open: gt, lt
  Comparator #(.width(3), .mode("unsigned")) comparator_23 (
    .a(func3), .b(3'b100), .eq(comparator_23_eq));  // open: gt, lt
  Comparator #(.width(3), .mode("unsigned")) comparator_24 (
    .a(func3), .b(3'b110), .eq(comparator_24_eq));  // open: gt, lt
  Comparator #(.width(3), .mode("unsigned")) comparator_25 (
    .a(func3), .b(3'b001), .eq(comparator_25_eq));  // open: gt, lt
  Comparator #(.width(7), .mode("unsigned")) comparator_26 (.a(Opcode), .b(7'b0110111), .eq(lui));  // open: gt, lt
  Comparator #(.width(7), .mode("unsigned")) comparator_27 (.a(Opcode), .b(7'b1101111), .eq(jal));  // open: gt, lt
  and and_13 (sw, s23_opcode, comparator_20_eq);
  and and_14 (beq, b63_opcode, comparator_22_eq);
  and and_15 (blt, b63_opcode, comparator_23_eq);
  and and_16 (bltu, b63_opcode, comparator_24_eq);
  and and_17 (bne, b63_opcode, comparator_25_eq);
  nor nor_1 (nor_1_out, addi, add, my_and, andi, my_or, ori, my_xor, xori, my_srl, srli, srai, lw, my_sll, slli, slt, slti, divu, remu, sub, lui, mul, mulh);
  Multiplexer #(.width(4), .enable("false")) multiplexer_15 (
    .in1(4'b0000), .out(alu_sel), .sel(nor_1_out));  // open: in0
  Comparator #(.width(3), .mode("unsigned")) comparator_28 (
    .a(func3), .b(3'b000), .eq(comparator_28_eq));  // open: gt, lt
  Comparator #(.width(7), .mode("unsigned")) comparator_29 (
    .a(func7), .b({7{1'b0}}), .eq(comparator_29_eq));  // open: gt, lt
  Comparator #(.width(3), .mode("unsigned")) comparator_30 (
    .a(func3), .b(3'b000), .eq(comparator_30_eq));  // open: gt, lt
  Comparator #(.width(7), .mode("unsigned")) comparator_31 (
    .a(func7), .b(7'b0000001), .eq(comparator_31_eq));  // open: gt, lt
  Comparator #(.width(3), .mode("unsigned")) comparator_32 (
    .a(func3), .b(3'b000), .eq(comparator_32_eq));  // open: gt, lt
  Comparator #(.width(7), .mode("unsigned")) comparator_33 (
    .a(func7), .b(7'b0100000), .eq(comparator_33_eq));  // open: gt, lt
  Comparator #(.width(3), .mode("unsigned")) comparator_34 (
    .a(func3), .b(3'b001), .eq(comparator_34_eq));  // open: gt, lt
  Comparator #(.width(7), .mode("unsigned")) comparator_35 (
    .a(func7), .b({7{1'b0}}), .eq(comparator_35_eq));  // open: gt, lt
  Comparator #(.width(3), .mode("unsigned")) comparator_36 (
    .a(func3), .b(3'b001), .eq(comparator_36_eq));  // open: gt, lt
  Comparator #(.width(7), .mode("unsigned")) comparator_37 (
    .a(func7), .b(7'b0000001), .eq(comparator_37_eq));  // open: gt, lt
  and and_18 (add, r33_opcode, comparator_28_eq, comparator_29_eq);
  and and_19 (mul, r33_opcode, comparator_30_eq, comparator_31_eq);
  and and_20 (sub, r33_opcode, comparator_32_eq, comparator_33_eq);
  and and_21 (my_sll, r33_opcode, comparator_34_eq, comparator_35_eq);
  and and_22 (mulh, r33_opcode, comparator_36_eq, comparator_37_eq);
  Comparator #(.width(3), .mode("unsigned")) comparator_38 (
    .a(func3), .b(3'b011), .eq(comparator_38_eq));  // open: gt, lt
  Comparator #(.width(7), .mode("unsigned")) comparator_39 (
    .a(func7), .b(7'b0000001), .eq(comparator_39_eq));  // open: gt, lt
  Comparator #(.width(3), .mode("unsigned")) comparator_40 (
    .a(func3), .b(3'b010), .eq(comparator_40_eq));  // open: gt, lt
  Comparator #(.width(7), .mode("unsigned")) comparator_41 (
    .a(func7), .b({7{1'b0}}), .eq(comparator_41_eq));  // open: gt, lt
  Comparator #(.width(3), .mode("unsigned")) comparator_42 (
    .a(func3), .b(3'b100), .eq(comparator_42_eq));  // open: gt, lt
  Comparator #(.width(7), .mode("unsigned")) comparator_43 (
    .a(func7), .b({7{1'b0}}), .eq(comparator_43_eq));  // open: gt, lt
  Comparator #(.width(3), .mode("unsigned")) comparator_44 (
    .a(func3), .b(3'b101), .eq(comparator_44_eq));  // open: gt, lt
  Comparator #(.width(7), .mode("unsigned")) comparator_45 (
    .a(func7), .b(7'b0000001), .eq(comparator_45_eq));  // open: gt, lt
  Comparator #(.width(3), .mode("unsigned")) comparator_46 (
    .a(func3), .b(3'b101), .eq(comparator_46_eq));  // open: gt, lt
  Comparator #(.width(7), .mode("unsigned")) comparator_47 (
    .a(func7), .b({7{1'b0}}), .eq(comparator_47_eq));  // open: gt, lt
  Comparator #(.width(7), .mode("unsigned")) comparator_48 (
    .a(Opcode), .b(7'b0110011), .eq(r33_opcode));  // open: gt, lt
  and and_23 (mulhu, r33_opcode, comparator_38_eq, comparator_39_eq);
  and and_24 (slt, r33_opcode, comparator_40_eq, comparator_41_eq);
  and and_25 (my_xor, r33_opcode, comparator_42_eq, comparator_43_eq);
  and and_26 (divu, r33_opcode, comparator_44_eq, comparator_45_eq);
  and and_27 (my_srl, r33_opcode, comparator_46_eq, comparator_47_eq);
  Comparator #(.width(3), .mode("unsigned")) comparator_49 (
    .a(func3), .b(3'b110), .eq(comparator_49_eq));  // open: gt, lt
  Comparator #(.width(7), .mode("unsigned")) comparator_50 (
    .a(func7), .b({7{1'b0}}), .eq(comparator_50_eq));  // open: gt, lt
  Comparator #(.width(3), .mode("unsigned")) comparator_51 (
    .a(func3), .b(3'b111), .eq(comparator_51_eq));  // open: gt, lt
  Comparator #(.width(7), .mode("unsigned")) comparator_52 (
    .a(func7), .b(7'b0000001), .eq(comparator_52_eq));  // open: gt, lt
  Comparator #(.width(3), .mode("unsigned")) comparator_53 (
    .a(func3), .b(3'b111), .eq(comparator_53_eq));  // open: gt, lt
  Comparator #(.width(7), .mode("unsigned")) comparator_54 (
    .a(func7), .b({7{1'b0}}), .eq(comparator_54_eq));  // open: gt, lt
  and and_28 (my_or, r33_opcode, comparator_49_eq, comparator_50_eq);
  and and_29 (remu, r33_opcode, comparator_51_eq, comparator_52_eq);
  and and_30 (my_and, r33_opcode, comparator_53_eq, comparator_54_eq);

  // Other names for the same wires on the sheet: inst_func3[2:0] = func3; inst_func7[6:0] = func7;
  //   inst_opcode[6:0] = Opcode

  // Notes on the sheet:
  //   Opcode 0x03
  //   Opcode 0x67
  //   Opcode 0x13
  //   Opcode 0x23
  //   Opcode 0x63
  //   Opcode 0x37
  //   Opcode 0x6f
  //   Func3 0x0
  //   Func3 0x1
  //   Func3 0x5
  //   Opcode 0x33
  //   Func3 0x7
endmodule

module B_Sel (
  input  [6:0] opcode,
  input  [2:0] func3,
  input  [6:0] func7,
  output Result
);

  wire and_1_out, and_2_out, and_3_out, and_6_out, and_7_out, and_8_out, and_9_out, and_10_out, and_11_out,
       and_12_out, and_13_out, and_14_out, and_15_out, and_16_out, and_17_out, b63_opcode, b_type_sel,
       comparator_1_eq, comparator_2_eq, comparator_3_eq, comparator_4_eq, comparator_5_eq, comparator_6_eq,
       comparator_7_eq, comparator_8_eq, comparator_9_eq, comparator_15_eq, comparator_16_eq,
       comparator_17_eq, comparator_18_eq, comparator_19_eq, comparator_22_eq, comparator_23_eq,
       comparator_24_eq, comparator_25_eq, comparator_26_eq, comparator_27_eq, i3, i3_opcode, i13,
       i13_opcode, i67, i67_opcode, i_ex, i_type_sel, j_type_sel, s23_opcode, s_type_sel, u_type_sel;

  Comparator #(.width(3), .mode("unsigned")) comparator_1 (
    .a(func3), .b(3'b000), .eq(comparator_1_eq));  // open: gt, lt
  Comparator #(.width(3), .mode("unsigned")) comparator_2 (
    .a(func3), .b(3'b001), .eq(comparator_2_eq));  // open: gt, lt
  Comparator #(.width(3), .mode("unsigned")) comparator_3 (
    .a(func3), .b(3'b010), .eq(comparator_3_eq));  // open: gt, lt
  Comparator #(.width(3), .mode("unsigned")) comparator_4 (
    .a(func3), .b(3'b000), .eq(comparator_4_eq));  // open: gt, lt
  Comparator #(.width(3), .mode("unsigned")) comparator_5 (
    .a(func3), .b(3'b010), .eq(comparator_5_eq));  // open: gt, lt
  Comparator #(.width(3), .mode("unsigned")) comparator_6 (
    .a(func3), .b(3'b000), .eq(comparator_6_eq));  // open: gt, lt
  Comparator #(.width(3), .mode("unsigned")) comparator_7 (
    .a(func3), .b(3'b100), .eq(comparator_7_eq));  // open: gt, lt
  Comparator #(.width(3), .mode("unsigned")) comparator_8 (
    .a(func3), .b(3'b110), .eq(comparator_8_eq));  // open: gt, lt
  Comparator #(.width(3), .mode("unsigned")) comparator_9 (
    .a(func3), .b(3'b001), .eq(comparator_9_eq));  // open: gt, lt
  Comparator #(.width(7), .mode("unsigned")) comparator_10 (
    .a(opcode), .b(7'b0000011), .eq(i3_opcode));  // open: gt, lt
  Comparator #(.width(7), .mode("unsigned")) comparator_11 (
    .a(opcode), .b(7'b1100111), .eq(i67_opcode));  // open: gt, lt
  Comparator #(.width(7), .mode("unsigned")) comparator_12 (
    .a(opcode), .b(7'b0100011), .eq(s23_opcode));  // open: gt, lt
  Comparator #(.width(7), .mode("unsigned")) comparator_13 (
    .a(opcode), .b(7'b1100011), .eq(b63_opcode));  // open: gt, lt
  and and_1 (and_1_out, i3_opcode, comparator_1_eq);
  and and_2 (and_2_out, i3_opcode, comparator_2_eq);
  and and_3 (and_3_out, i3_opcode, comparator_3_eq);
  and and_4 (i67, i67_opcode, comparator_4_eq);
  and and_5 (s_type_sel, s23_opcode, comparator_5_eq);
  and and_6 (and_6_out, b63_opcode, comparator_6_eq);
  and and_7 (and_7_out, b63_opcode, comparator_7_eq);
  and and_8 (and_8_out, b63_opcode, comparator_8_eq);
  and and_9 (and_9_out, b63_opcode, comparator_9_eq);
  or or_1 (i3, and_1_out, and_2_out, and_3_out);
  or or_2 (b_type_sel, and_6_out, and_7_out, and_8_out, and_9_out);
  Comparator #(.width(7), .mode("unsigned")) comparator_14 (
    .a(opcode), .b(7'b0010011), .eq(i13_opcode));  // open: gt, lt
  Comparator #(.width(3), .mode("unsigned")) comparator_15 (
    .a(func3), .b(3'b000), .eq(comparator_15_eq));  // open: gt, lt
  Comparator #(.width(3), .mode("unsigned")) comparator_16 (
    .a(func3), .b(3'b010), .eq(comparator_16_eq));  // open: gt, lt
  Comparator #(.width(3), .mode("unsigned")) comparator_17 (
    .a(func3), .b(3'b100), .eq(comparator_17_eq));  // open: gt, lt
  Comparator #(.width(3), .mode("unsigned")) comparator_18 (
    .a(func3), .b(3'b110), .eq(comparator_18_eq));  // open: gt, lt
  Comparator #(.width(3), .mode("unsigned")) comparator_19 (
    .a(func3), .b(3'b111), .eq(comparator_19_eq));  // open: gt, lt
  Comparator #(.width(7), .mode("unsigned")) comparator_20 (
    .a(opcode), .b(7'b0110111), .eq(u_type_sel));  // open: gt, lt
  Comparator #(.width(7), .mode("unsigned")) comparator_21 (
    .a(opcode), .b(7'b1101111), .eq(j_type_sel));  // open: gt, lt
  and and_10 (and_10_out, i13_opcode, comparator_15_eq);
  and and_11 (and_11_out, i13_opcode, comparator_16_eq);
  and and_12 (and_12_out, i13_opcode, comparator_17_eq);
  and and_13 (and_13_out, i13_opcode, comparator_18_eq);
  and and_14 (and_14_out, i13_opcode, comparator_19_eq);
  or or_3 (i13, and_10_out, and_11_out, and_12_out, and_13_out, and_14_out);
  or or_4 (i_type_sel, i3, i13, i67);
  or or_5 (Result, i_type_sel, s_type_sel, b_type_sel, u_type_sel, j_type_sel, i_ex);
  Comparator #(.width(3), .mode("unsigned")) comparator_22 (
    .a(func3), .b(3'b001), .eq(comparator_22_eq));  // open: gt, lt
  Comparator #(.width(7), .mode("unsigned")) comparator_23 (
    .a(func7), .b({7{1'b0}}), .eq(comparator_23_eq));  // open: gt, lt
  Comparator #(.width(3), .mode("unsigned")) comparator_24 (
    .a(func3), .b(3'b101), .eq(comparator_24_eq));  // open: gt, lt
  Comparator #(.width(7), .mode("unsigned")) comparator_25 (
    .a(func7), .b({7{1'b0}}), .eq(comparator_25_eq));  // open: gt, lt
  Comparator #(.width(3), .mode("unsigned")) comparator_26 (
    .a(func3), .b(3'b101), .eq(comparator_26_eq));  // open: gt, lt
  Comparator #(.width(7), .mode("unsigned")) comparator_27 (
    .a(func7), .b(7'b0100000), .eq(comparator_27_eq));  // open: gt, lt
  and and_15 (and_15_out, i13_opcode, comparator_22_eq, comparator_23_eq);
  and and_16 (and_16_out, i13_opcode, comparator_24_eq, comparator_25_eq);
  and and_17 (and_17_out, i13_opcode, comparator_26_eq, comparator_27_eq);
  or or_6 (i_ex, and_15_out, and_16_out, and_17_out);

  // Notes on the sheet:
  //   I-exceptions
endmodule

module PCSel (
  input  [6:0] Opcode,
  input  [2:0] func3,
  input  [6:0] func7,
  input  BrEq,
  input  BrLt,
  output out_6
);

  wire and_1_out, and_2_out, and_3_out, and_4_out, and_5_out, b63_opcode, b67_opcode, comparator_2_eq,
       comparator_3_eq, comparator_4_eq, comparator_5_eq, comparator_6_eq, comparator_8_eq, not_1_out;

  Comparator #(.width(7), .mode("unsigned")) comparator_1 (
    .a(Opcode), .b(7'b1100111), .eq(b67_opcode));  // open: gt, lt
  Comparator #(.width(3), .mode("unsigned")) comparator_2 (
    .a(func3), .b(3'b000), .eq(comparator_2_eq));  // open: gt, lt
  Comparator #(.width(3), .mode("unsigned")) comparator_3 (
    .a(func3), .b(3'b000), .eq(comparator_3_eq));  // open: gt, lt
  Comparator #(.width(3), .mode("unsigned")) comparator_4 (
    .a(func3), .b(3'b100), .eq(comparator_4_eq));  // open: gt, lt
  Comparator #(.width(3), .mode("unsigned")) comparator_5 (
    .a(func3), .b(3'b110), .eq(comparator_5_eq));  // open: gt, lt
  Comparator #(.width(3), .mode("unsigned")) comparator_6 (
    .a(func3), .b(3'b001), .eq(comparator_6_eq));  // open: gt, lt
  Comparator #(.width(7), .mode("unsigned")) comparator_7 (
    .a(Opcode), .b(7'b1100011), .eq(b63_opcode));  // open: gt, lt
  not not_1 (not_1_out, BrEq);
  Comparator #(.width(7), .mode("unsigned")) comparator_8 (
    .a(Opcode), .b(7'b1101111), .eq(comparator_8_eq));  // open: gt, lt
  and and_1 (and_1_out, b67_opcode, comparator_2_eq);
  and and_2 (and_2_out, b63_opcode, BrEq, comparator_3_eq);
  and and_3 (and_3_out, b63_opcode, BrLt, comparator_4_eq);
  and and_4 (and_4_out, b63_opcode, BrLt, comparator_5_eq);
  and and_5 (and_5_out, b63_opcode, not_1_out, comparator_6_eq);
  or or_1 (out_6, and_2_out, and_3_out, and_4_out, and_5_out, comparator_8_eq, and_1_out);

  // Other names for the same wires on the sheet: Result = out_6
endmodule

module ASel (
  input  [6:0] opcode,
  input  [2:0] func3,
  input  [6:0] func7,
  output out_4
);

  wire and_1_out, and_2_out, and_3_out, and_4_out, b63_opcode, comparator_1_eq, comparator_2_eq,
       comparator_3_eq, comparator_4_eq, comparator_5_eq;

  Comparator #(.width(3), .mode("unsigned")) comparator_1 (
    .a(func3), .b(3'b000), .eq(comparator_1_eq));  // open: gt, lt
  Comparator #(.width(3), .mode("unsigned")) comparator_2 (
    .a(func3), .b(3'b100), .eq(comparator_2_eq));  // open: gt, lt
  Comparator #(.width(3), .mode("unsigned")) comparator_3 (
    .a(func3), .b(3'b110), .eq(comparator_3_eq));  // open: gt, lt
  Comparator #(.width(3), .mode("unsigned")) comparator_4 (
    .a(func3), .b(3'b001), .eq(comparator_4_eq));  // open: gt, lt
  Comparator #(.width(7), .mode("unsigned")) comparator_5 (
    .a(opcode), .b(7'b1101111), .eq(comparator_5_eq));  // open: gt, lt
  Comparator #(.width(7), .mode("unsigned")) comparator_6 (
    .a(opcode), .b(7'b1100011), .eq(b63_opcode));  // open: gt, lt
  and and_1 (and_1_out, b63_opcode, comparator_1_eq);
  and and_2 (and_2_out, b63_opcode, comparator_2_eq);
  and and_3 (and_3_out, b63_opcode, comparator_3_eq);
  and and_4 (and_4_out, b63_opcode, comparator_4_eq);
  or or_1 (out_4, and_1_out, and_2_out, and_3_out, and_4_out, comparator_5_eq);

  // Other names for the same wires on the sheet: Result = out_4
endmodule

module WBSel (
  input  [6:0] opcode,
  input  [2:0] func3,
  input  [6:0] func7,
  output [1:0] out_4
);

  wire and_2_out, comparator_1_eq, comparator_4_eq, comparator_5_eq, i03_opcode, i67_opcode, jumps, lw,
       nor_1_out;

  Multiplexer #(.width(2), .enable("false")) multiplexer_1 (.in1(2'b00), .out(out_4), .sel(lw));  // open: in0
  Multiplexer #(.width(2), .enable("false")) multiplexer_2 (.in1(2'b10), .out(out_4), .sel(jumps));  // open: in0
  nor nor_1 (nor_1_out, lw, jumps);
  Multiplexer #(.width(2), .enable("false")) multiplexer_3 (.in1(2'b01), .out(out_4), .sel(nor_1_out));  // open: in0
  Comparator #(.width(3), .mode("unsigned")) comparator_1 (
    .a(func3), .b(3'b010), .eq(comparator_1_eq));  // open: gt, lt
  Comparator #(.width(7), .mode("unsigned")) comparator_2 (
    .a(opcode), .b(7'b0000011), .eq(i03_opcode));  // open: gt, lt
  Comparator #(.width(7), .mode("unsigned")) comparator_3 (
    .a(opcode), .b(7'b1100111), .eq(i67_opcode));  // open: gt, lt
  Comparator #(.width(3), .mode("unsigned")) comparator_4 (
    .a(func3), .b(3'b000), .eq(comparator_4_eq));  // open: gt, lt
  Comparator #(.width(7), .mode("unsigned")) comparator_5 (
    .a(opcode), .b(7'b1101111), .eq(comparator_5_eq));  // open: gt, lt
  and and_1 (lw, i03_opcode, comparator_1_eq);
  and and_2 (and_2_out, i67_opcode, comparator_4_eq);
  or or_1 (jumps, and_2_out, comparator_5_eq);

  // Other names for the same wires on the sheet: Result[1:0] = out_4

  // Notes on the sheet:
  //   WBSel = 0 if LW
endmodule

module nop (
  output [31:0] out_1
);


  assign out_1 = 32'h13;
endmodule

module isBranch (
  input  [6:0] opcode,
  input  [2:0] func3,
  input  [6:0] func7,
  output out_4
);

  wire and_1_out, and_2_out, and_3_out, and_4_out, b63_opcode, comparator_1_eq, comparator_2_eq,
       comparator_3_eq, comparator_4_eq;

  Comparator #(.width(3), .mode("unsigned")) comparator_1 (
    .a(func3), .b(3'b000), .eq(comparator_1_eq));  // open: gt, lt
  Comparator #(.width(3), .mode("unsigned")) comparator_2 (
    .a(func3), .b(3'b100), .eq(comparator_2_eq));  // open: gt, lt
  Comparator #(.width(3), .mode("unsigned")) comparator_3 (
    .a(func3), .b(3'b110), .eq(comparator_3_eq));  // open: gt, lt
  Comparator #(.width(3), .mode("unsigned")) comparator_4 (
    .a(func3), .b(3'b001), .eq(comparator_4_eq));  // open: gt, lt
  Comparator #(.width(7), .mode("unsigned")) comparator_5 (
    .a(opcode), .b(7'b1100011), .eq(b63_opcode));  // open: gt, lt
  and and_1 (and_1_out, b63_opcode, comparator_1_eq);
  and and_2 (and_2_out, b63_opcode, comparator_2_eq);
  and and_3 (and_3_out, b63_opcode, comparator_3_eq);
  and and_4 (and_4_out, b63_opcode, comparator_4_eq);
  or or_1 (out_4, and_1_out, and_2_out, and_3_out, and_4_out);

  // Other names for the same wires on the sheet: Result = out_4
endmodule

module instru_decode (
  input  [31:0] instruction,
  output [6:0] opcode,
  output [4:0] rd,
  output [2:0] func3,
  output [4:0] rs1,
  output [11:0] imm,
  output [4:0] rs2,
  output [6:0] func7
);


  assign func3 = instruction[14:12];
  assign func7 = instruction[31:25];
  assign imm = instruction[31:20];
  assign opcode = instruction[6:0];
  assign rd = instruction[11:7];
  assign rs1 = instruction[19:15];
  assign rs2 = instruction[24:20];
endmodule

module Branch_Comp (
  input  [6:0] opcode,
  input  [2:0] func3,
  input  [31:0] RegA,
  input  [31:0] RegB,
  output BrEq,
  output BLT
);

  wire b63_opcode, comparator_3_eq, signed_BrEq, signed_BrLt, signed_comp, unsigned_BrEq, unsigned_BrLt;

  Comparator #(.width(32)) comparator_1 (.a(RegA), .b(RegB), .eq(signed_BrEq), .lt(signed_BrLt));  // open: gt
  Multiplexer #(.enable("false")) multiplexer_1 (.in0(unsigned_BrEq), .in1(signed_BrEq), .out(BrEq), .sel(signed_comp));
  Comparator #(.width(7), .mode("unsigned")) comparator_2 (
    .a(opcode), .b(7'b1100011), .eq(b63_opcode));  // open: gt, lt
  Comparator #(.width(3), .mode("unsigned")) comparator_3 (
    .a(func3), .b(3'b100), .eq(comparator_3_eq));  // open: gt, lt
  and and_1 (signed_comp, b63_opcode, comparator_3_eq);
  Comparator #(.width(32), .mode("unsigned")) comparator_4 (
    .a(RegA), .b(RegB), .eq(unsigned_BrEq), .lt(unsigned_BrLt));  // open: gt
  Multiplexer #(.enable("false")) multiplexer_2 (.in0(unsigned_BrLt), .in1(signed_BrLt), .out(BLT), .sel(signed_comp));
  // NOT_Gate not_1 is placed but not wired

  // Other names for the same wires on the sheet: A[31:0] = RegA; B[31:0] = RegB; BrEq_result = BrEq;
  //   BrLt_result = BLT
endmodule
