// Logisim project cpucontrol.circ as structural Verilog: 5 circuits, main circuit main
module main (
  input  [31:0] INSTRUCTION,
  input  CLOCK,
  output [31:0] PROGRAM_COUNTER,
  output [31:0] ra,
  output [31:0] sp,
  output [31:0] t0,
  output [31:0] t1,
  output [31:0] t2,
  output [31:0] s0,
  output [31:0] s1,
  output [31:0] a0
);

  wire asel, bsel_addi, comparator_1_eq, comparator_2_eq, comparator_3_eq, comparator_4_eq, comparator_5_eq,
       comparator_6_eq, comparator_7_eq, comparator_8_eq, comparator_9_eq, comparator_10_eq,
       comparator_11_eq, myEnable;
  wire [2:0] func3;
  wire [4:0] imm, instruction_t;
  wire [6:0] func7, opcode;
  wire [19:7] pipe_instr;
  wire [31:0] adder_1_out, alu_result, multiplexer_1_out, RegFile_read_data_1, RegFile_read_data_2;

  Adder #(.width(32)) adder_1 (.a(PROGRAM_COUNTER), .b(32'h4), .out(adder_1_out));  // open: cin, cout
  Register #(.width(32)) PC (.D(adder_1_out), .clk(CLOCK), .Q(PROGRAM_COUNTER));  // open: en, clr
  Register #(.width(32)) instr_ID ();  // open: D, en, Q, clk, clr
  Register #(.width(32)) pipelined (
    .D(INSTRUCTION), .en(1'b1), .clk(CLOCK),
    .Q({func7, imm, pipe_instr[19:15], func3, pipe_instr[11:7], opcode}));  // open: clr
  Comparator #(.width(7)) comparator_1 (.a(opcode), .b(7'b0010011), .eq(comparator_1_eq));  // open: gt, lt
  Comparator #(.width(3)) comparator_2 (.a(func3), .b(3'b000), .eq(comparator_2_eq));  // open: gt, lt
  Comparator #(.width(7)) comparator_3 (.a(opcode), .b(7'b1101111), .eq(comparator_3_eq));  // open: gt, lt
  Comparator #(.width(7)) comparator_4 (.a(opcode), .b(7'b1100111), .eq(comparator_4_eq));  // open: gt, lt
  and and_1 (asel, comparator_3_eq, comparator_4_eq);
  regfile_main RegFile (
    .rs2(imm), .rd(pipe_instr[11:7]), .Read_Data_1(RegFile_read_data_1), .Read_Data_2(RegFile_read_data_2),
    .ra(ra), .sp(sp), .t0(t0), .t1(t1), .t2(t2), .s0(s0), .s1(s1), .a0(a0), .rs1(pipe_instr[19:15]),
    .Write_Data(alu_result), .RegWEn(myEnable), .clk(CLOCK));
  and and_2 (bsel_addi, comparator_1_eq, comparator_2_eq);
  Register #(.width(32)) PC_EX ();  // open: D, en, Q, clk, clr
  Register #(.width(32)) rs1_EX ();  // open: D, en, Q, clk, clr
  Register #(.width(32)) rs2_EX ();  // open: D, en, Q, clk, clr
  Register #(.width(32)) imm_EX ();  // open: D, en, Q, clk, clr
  Register #(.width(32)) PC_MEM ();  // open: D, en, Q, clk, clr
  Register #(.width(32)) rs2_MEM ();  // open: D, en, Q, clk, clr
  Register #(.width(32)) ALU_out_MEM ();  // open: D, en, Q, clk, clr
  Multiplexer #(.width(32), .enable("false")) multiplexer_1 (
    .in0(RegFile_read_data_2), .in1({{20{1'b0}}, func7, imm}), .out(multiplexer_1_out), .sel(bsel_addi));
  Comparator #(.width(7), .mode("unsigned")) comparator_5 (
    .a(opcode), .b(7'b0000011), .eq(comparator_5_eq));  // open: gt, lt
  Comparator #(.width(7), .mode("unsigned")) comparator_6 (
    .a(opcode), .b(7'b0010011), .eq(comparator_6_eq));  // open: gt, lt
  Comparator #(.width(7), .mode("unsigned")) comparator_7 (
    .a(opcode), .b(7'b1110011), .eq(comparator_7_eq));  // open: gt, lt
  Comparator #(.width(7), .mode("unsigned")) comparator_8 (
    .a(opcode), .b(7'b0110011), .eq(comparator_8_eq));  // open: gt, lt
  Comparator #(.width(7), .mode("unsigned")) comparator_9 (
    .a(opcode), .b(7'b0011011), .eq(comparator_9_eq));  // open: gt, lt
  Comparator #(.width(7), .mode("unsigned")) comparator_10 (
    .a(opcode), .b(7'b0111011), .eq(comparator_10_eq));  // open: gt, lt
  Comparator #(.width(7), .mode("unsigned")) comparator_11 (
    .a(opcode), .b(7'b1100111), .eq(comparator_11_eq));  // open: gt, lt
  // alu Arithmetic_Logic_Unit: pin names not known; wires that end beside it: RegFile_read_data_1, multiplexer_1_out, instruction_t, alu_result
  // mem_main DMEM: pin names not known
  or or_1 (myEnable, comparator_5_eq, comparator_6_eq, comparator_7_eq, comparator_8_eq, comparator_9_eq, comparator_10_eq, comparator_11_eq);

  // Other names for the same wires on the sheet: clk = CLOCK; imm_ext[11:0] = {func7, imm};
  //   pipe_instr (some bits) = {func7, imm, func3, opcode}; rs2[4:0] = imm; imm[11:5] = func7;
  //   rd[4:0] = pipe_instr[11:7]; rs1[4:0] = pipe_instr[19:15]

  // Notes on the sheet:
  //   Output
  //   Instruction Decode
  //   IMEM (do **NOT** move this)
  //   Inputs
  //   Imm Sign Extention
  //   It is OK to move the PC, RegFile, ALU, and MEM to wherever is most convenient for you when constructing your CPU, and to delete this text
  //   Inputs/Outputs for testing. Do **NOT** move these.
  //   RegWen
endmodule

module instructions (
  input  [6:0] in_1,
  input  [2:0] in_2,
  input  [6:0] in_3
);

  wire add, and_1_out, and_2_out, and_4_out, and_8_out, and_10_out, and_12_out, and_13_out, and_15_out,
       and_17_out, and_19_out, and_22_out, and_24_out, and_26_out, comparator_1_eq, comparator_2_eq,
       comparator_3_eq, comparator_4_eq, comparator_5_eq, comparator_6_eq, comparator_7_eq, comparator_8_eq,
       comparator_9_eq, comparator_10_eq, comparator_11_eq, comparator_12_eq, comparator_13_eq,
       comparator_14_eq, comparator_15_eq, comparator_16_eq, comparator_17_eq, comparator_18_eq,
       comparator_19_eq, comparator_20_eq, comparator_21_eq, comparator_22_eq, comparator_23_eq,
       comparator_24_eq, comparator_25_eq, comparator_26_eq, comparator_27_eq, comparator_28_eq,
       comparator_29_eq, comparator_30_eq, comparator_31_eq, comparator_32_eq, comparator_33_eq,
       comparator_34_eq, comparator_35_eq, comparator_36_eq, comparator_37_eq, comparator_38_eq,
       comparator_39_eq, divu, mul, mulh, mulhu, pand, por, psll, psrl, pxor, remu, slt, sub;

  instructions2 instructions2_1 ();  // open: in_1, in_2, in_3
  Comparator #(.width(3)) comparator_1 (.a(in_2), .b(3'b000), .eq(comparator_1_eq));  // open: gt, lt
  Comparator #(.width(7)) comparator_2 (.a(in_3), .b({7{1'b0}}), .eq(comparator_2_eq));  // open: gt, lt
  Comparator #(.width(7)) comparator_3 (.a(in_1), .b(7'b0110011), .eq(comparator_3_eq));  // open: gt, lt
  Comparator #(.width(3)) comparator_4 (.a(in_2), .b(3'b001), .eq(comparator_4_eq));  // open: gt, lt
  Comparator #(.width(7)) comparator_5 (.a(in_3), .b({7{1'b0}}), .eq(comparator_5_eq));  // open: gt, lt
  Comparator #(.width(7)) comparator_6 (.a(in_1), .b(7'b0110011), .eq(comparator_6_eq));  // open: gt, lt
  Comparator #(.width(3)) comparator_7 (.a(in_2), .b(3'b010), .eq(comparator_7_eq));  // open: gt, lt
  Comparator #(.width(7)) comparator_8 (.a(in_3), .b({7{1'b0}}), .eq(comparator_8_eq));  // open: gt, lt
  Comparator #(.width(7)) comparator_9 (.a(in_1), .b(7'b0110011), .eq(comparator_9_eq));  // open: gt, lt
  and and_1 (and_1_out, comparator_1_eq, comparator_2_eq);
  and and_2 (and_2_out, comparator_4_eq, comparator_5_eq);
  and and_3 (slt, comparator_6_eq, and_4_out);
  and and_4 (and_4_out, comparator_7_eq, comparator_8_eq);
  and and_5 (add, comparator_9_eq, and_1_out);
  and and_6 (psll, comparator_3_eq, and_2_out);
  Comparator #(.width(7)) comparator_10 (.a(in_1), .b(7'b0110011), .eq(comparator_10_eq));  // open: gt, lt
  Comparator #(.width(3)) comparator_11 (.a(in_2), .b(3'b000), .eq(comparator_11_eq));  // open: gt, lt
  Comparator #(.width(7)) comparator_12 (.a(in_3), .b(7'b0000001), .eq(comparator_12_eq));  // open: gt, lt
  Comparator #(.width(7)) comparator_13 (.a(in_1), .b(7'b0110011), .eq(comparator_13_eq));  // open: gt, lt
  Comparator #(.width(3)) comparator_14 (.a(in_2), .b(3'b001), .eq(comparator_14_eq));  // open: gt, lt
  Comparator #(.width(7)) comparator_15 (.a(in_3), .b({7{1'b0}}), .eq(comparator_15_eq));  // open: gt, lt
  Comparator #(.width(7)) comparator_16 (.a(in_1), .b(7'b0110011), .eq(comparator_16_eq));  // open: gt, lt
  Comparator #(.width(3)) comparator_17 (.a(in_2), .b(3'b100), .eq(comparator_17_eq));  // open: gt, lt
  Comparator #(.width(7)) comparator_18 (.a(in_3), .b({7{1'b0}}), .eq(comparator_18_eq));  // open: gt, lt
  and and_7 (mul, comparator_10_eq, and_8_out);
  and and_8 (and_8_out, comparator_11_eq, comparator_12_eq);
  and and_9 (mulh, comparator_13_eq, and_10_out);
  and and_10 (and_10_out, comparator_14_eq, comparator_15_eq);
  and and_11 (pxor, comparator_16_eq, and_12_out);
  and and_12 (and_12_out, comparator_17_eq, comparator_18_eq);
  Comparator #(.width(3)) comparator_19 (.a(in_2), .b(3'b010), .eq(comparator_19_eq));  // open: gt, lt
  Comparator #(.width(7)) comparator_20 (.a(in_3), .b({7{1'b0}}), .eq(comparator_20_eq));  // open: gt, lt
  Comparator #(.width(7)) comparator_21 (.a(in_1), .b(7'b0110011), .eq(comparator_21_eq));  // open: gt, lt
  Comparator #(.width(3)) comparator_22 (.a(in_2), .b(3'b000), .eq(comparator_22_eq));  // open: gt, lt
  Comparator #(.width(7)) comparator_23 (.a(in_3), .b(7'b0100000), .eq(comparator_23_eq));  // open: gt, lt
  Comparator #(.width(7)) comparator_24 (.a(in_1), .b(7'b0110011), .eq(comparator_24_eq));  // open: gt, lt
  Comparator #(.width(3)) comparator_25 (.a(in_2), .b(3'b011), .eq(comparator_25_eq));  // open: gt, lt
  Comparator #(.width(7)) comparator_26 (.a(in_3), .b(7'b0000001), .eq(comparator_26_eq));  // open: gt, lt
  Comparator #(.width(7)) comparator_27 (.a(in_1), .b(7'b0110011), .eq(comparator_27_eq));  // open: gt, lt
  Comparator #(.width(3)) comparator_28 (.a(in_2), .b(3'b101), .eq(comparator_28_eq));  // open: gt, lt
  Comparator #(.width(7)) comparator_29 (.a(in_3), .b(7'b0000001), .eq(comparator_29_eq));  // open: gt, lt
  Comparator #(.width(7)) comparator_30 (.a(in_1), .b(7'b0110011), .eq(comparator_30_eq));  // open: gt, lt
  and and_13 (and_13_out, comparator_19_eq, comparator_20_eq);
  and and_14 (sub, comparator_21_eq, and_15_out);
  and and_15 (and_15_out, comparator_22_eq, comparator_23_eq);
  and and_16 (mulhu, comparator_24_eq, and_17_out);
  and and_17 (and_17_out, comparator_25_eq, comparator_26_eq);
  and and_18 (divu, comparator_27_eq, and_19_out);
  and and_19 (and_19_out, comparator_28_eq, comparator_29_eq);
  and and_20 (remu, comparator_30_eq, and_13_out);
  Comparator #(.width(7)) comparator_31 (.a(in_1), .b(7'b0110011), .eq(comparator_31_eq));  // open: gt, lt
  Comparator #(.width(3)) comparator_32 (.a(in_2), .b(3'b010), .eq(comparator_32_eq));  // open: gt, lt
  Comparator #(.width(7)) comparator_33 (.a(in_3), .b({7{1'b0}}), .eq(comparator_33_eq));  // open: gt, lt
  Comparator #(.width(7)) comparator_34 (.a(in_1), .b(7'b0110011), .eq(comparator_34_eq));  // open: gt, lt
  Comparator #(.width(3)) comparator_35 (.a(in_2), .b(3'b010), .eq(comparator_35_eq));  // open: gt, lt
  Comparator #(.width(7)) comparator_36 (.a(in_3), .b({7{1'b0}}), .eq(comparator_36_eq));  // open: gt, lt
  Comparator #(.width(7)) comparator_37 (.a(in_1), .b(7'b0110011), .eq(comparator_37_eq));  // open: gt, lt
  Comparator #(.width(3)) comparator_38 (.a(in_2), .b(3'b111), .eq(comparator_38_eq));  // open: gt, lt
  Comparator #(.width(7)) comparator_39 (.a(in_3), .b(7'b0000001), .eq(comparator_39_eq));  // open: gt, lt
  and and_21 (psrl, comparator_31_eq, and_22_out);
  and and_22 (and_22_out, comparator_32_eq, comparator_33_eq);
  and and_23 (por, comparator_34_eq, and_24_out);
  and and_24 (and_24_out, comparator_35_eq, comparator_36_eq);
  and and_25 (pand, comparator_37_eq, and_26_out);
  and and_26 (and_26_out, comparator_38_eq, comparator_39_eq);

  // Other names for the same wires on the sheet: func3[2:0] = in_2; func7[6:0] = in_3; opcode[6:0] = in_1
endmodule

module instructions2 (
  input  [6:0] in_1,
  input  [2:0] in_2,
  input  [6:0] in_3
);

  wire addi, and_3_out, and_10_out, andi, comparator_1_eq, comparator_2_eq, comparator_3_eq, comparator_4_eq,
       comparator_5_eq, comparator_6_eq, comparator_7_eq, comparator_8_eq, comparator_9_eq, comparator_10_eq,
       comparator_11_eq, comparator_12_eq, comparator_13_eq, comparator_14_eq, comparator_15_eq,
       comparator_16_eq, comparator_17_eq, comparator_18_eq, comparator_19_eq, comparator_20_eq,
       comparator_21_eq, comparator_22_eq, comparator_23_eq, comparator_24_eq, jalr, lb, lh, lw, ori, slli,
       slti, srli, xori;

  Comparator #(.width(3)) comparator_1 (.a(in_2), .b(3'b000), .eq(comparator_1_eq));  // open: gt, lt
  Comparator #(.width(7)) comparator_2 (.a(in_1), .b(7'b0010011), .eq(comparator_2_eq));  // open: gt, lt
  Comparator #(.width(3)) comparator_3 (.a(in_2), .b(3'b000), .eq(comparator_3_eq));  // open: gt, lt
  Comparator #(.width(7)) comparator_4 (.a(in_1), .b(7'b0010011), .eq(comparator_4_eq));  // open: gt, lt
  Comparator #(.width(3)) comparator_5 (.a(in_2), .b(3'b110), .eq(comparator_5_eq));  // open: gt, lt
  Comparator #(.width(7)) comparator_6 (.a(in_1), .b(7'b0010011), .eq(comparator_6_eq));  // open: gt, lt
  Comparator #(.width(3)) comparator_7 (.a(in_2), .b(3'b001), .eq(comparator_7_eq));  // open: gt, lt
  Comparator #(.width(7)) comparator_8 (.a(in_3), .b({7{1'b0}}), .eq(comparator_8_eq));  // open: gt, lt
  Comparator #(.width(7)) comparator_9 (.a(in_1), .b(7'b0000011), .eq(comparator_9_eq));  // open: gt, lt
  and and_1 (ori, comparator_4_eq, comparator_5_eq);
  and and_2 (slli, comparator_6_eq, and_3_out);
  and and_3 (and_3_out, comparator_7_eq, comparator_8_eq);
  and and_4 (lb, comparator_9_eq, comparator_1_eq);
  and and_5 (addi, comparator_2_eq, comparator_3_eq);
  Comparator #(.width(7)) comparator_10 (.a(in_1), .b(7'b0000011), .eq(comparator_10_eq));  // open: gt, lt
  Comparator #(.width(3)) comparator_11 (.a(in_2), .b(3'b001), .eq(comparator_11_eq));  // open: gt, lt
  Comparator #(.width(7)) comparator_12 (.a(in_1), .b(7'b0010011), .eq(comparator_12_eq));  // open: gt, lt
  Comparator #(.width(3)) comparator_13 (.a(in_2), .b(3'b010), .eq(comparator_13_eq));  // open: gt, lt
  Comparator #(.width(7)) comparator_14 (.a(in_1), .b(7'b0010011), .eq(comparator_14_eq));  // open: gt, lt
  Comparator #(.width(3)) comparator_15 (.a(in_2), .b(3'b111), .eq(comparator_15_eq));  // open: gt, lt
  Comparator #(.width(7)) comparator_16 (.a(in_1), .b(7'b0010011), .eq(comparator_16_eq));  // open: gt, lt
  Comparator #(.width(3)) comparator_17 (.a(in_2), .b(3'b101), .eq(comparator_17_eq));  // open: gt, lt
  Comparator #(.width(7)) comparator_18 (.a(in_3), .b({7{1'b0}}), .eq(comparator_18_eq));  // open: gt, lt
  Comparator #(.width(7)) comparator_19 (.a(in_1), .b(7'b1100111), .eq(comparator_19_eq));  // open: gt, lt
  Comparator #(.width(3)) comparator_20 (.a(in_2), .b(3'b000), .eq(comparator_20_eq));  // open: gt, lt
  and and_6 (lh, comparator_10_eq, comparator_11_eq);
  and and_7 (slti, comparator_12_eq, comparator_13_eq);
  and and_8 (andi, comparator_14_eq, comparator_15_eq);
  and and_9 (srli, comparator_16_eq, and_10_out);
  and and_10 (and_10_out, comparator_17_eq, comparator_18_eq);
  and and_11 (jalr, comparator_19_eq, comparator_20_eq);
  Comparator #(.width(3)) comparator_21 (.a(in_2), .b(3'b100), .eq(comparator_21_eq));  // open: gt, lt
  Comparator #(.width(7)) comparator_22 (.a(in_1), .b(7'b0000011), .eq(comparator_22_eq));  // open: gt, lt
  Comparator #(.width(3)) comparator_23 (.a(in_2), .b(3'b010), .eq(comparator_23_eq));  // open: gt, lt
  Comparator #(.width(7)) comparator_24 (.a(in_1), .b(7'b0010011), .eq(comparator_24_eq));  // open: gt, lt
  and and_12 (lw, comparator_22_eq, comparator_23_eq);
  and and_13 (xori, comparator_24_eq, comparator_21_eq);

  // Other names for the same wires on the sheet: func3[2:0] = in_2; func7[6:0] = in_3; opcode[6:0] = in_1
endmodule

module instructions3 (
  input  [6:0] in_1,
  input  [2:0] in_2
);

  wire beq, blt, bltu, bne, comparator_1_eq, comparator_2_eq, comparator_3_eq, comparator_4_eq,
       comparator_5_eq, comparator_6_eq, comparator_9_eq, comparator_10_eq, comparator_11_eq,
       comparator_12_eq, jal, lui, sw;

  Comparator #(.width(3)) comparator_1 (.a(in_2), .b(3'b000), .eq(comparator_1_eq));  // open: gt, lt
  Comparator #(.width(3)) comparator_2 (.a(in_2), .b(3'b110), .eq(comparator_2_eq));  // open: gt, lt
  Comparator #(.width(7)) comparator_3 (.a(in_1), .b(7'b0100011), .eq(comparator_3_eq));  // open: gt, lt
  Comparator #(.width(3)) comparator_4 (.a(in_2), .b(3'b010), .eq(comparator_4_eq));  // open: gt, lt
  Comparator #(.width(7)) comparator_5 (.a(in_1), .b(7'b1100011), .eq(comparator_5_eq));  // open: gt, lt
  Comparator #(.width(7)) comparator_6 (.a(in_1), .b(7'b1100011), .eq(comparator_6_eq));  // open: gt, lt
  and and_1 (sw, comparator_3_eq, comparator_4_eq);
  and and_2 (beq, comparator_5_eq, comparator_1_eq);
  and and_3 (bltu, comparator_6_eq, comparator_2_eq);
  Comparator #(.width(7)) comparator_7 (.a(in_1), .b(7'b0110111), .eq(lui));  // open: gt, lt
  Comparator #(.width(7)) comparator_8 (.a(in_1), .b(7'b1101111), .eq(jal));  // open: gt, lt
  Comparator #(.width(7)) comparator_9 (.a(in_1), .b(7'b1100011), .eq(comparator_9_eq));  // open: gt, lt
  Comparator #(.width(3)) comparator_10 (.a(in_2), .b(3'b100), .eq(comparator_10_eq));  // open: gt, lt
  Comparator #(.width(7)) comparator_11 (.a(in_1), .b(7'b1100011), .eq(comparator_11_eq));  // open: gt, lt
  Comparator #(.width(3)) comparator_12 (.a(in_2), .b(3'b001), .eq(comparator_12_eq));  // open: gt, lt
  and and_4 (blt, comparator_9_eq, comparator_10_eq);
  and and_5 (bne, comparator_11_eq, comparator_12_eq);

  // Other names for the same wires on the sheet: func3[2:0] = in_2; opcode[6:0] = in_1
endmodule

module TheMatrix (
  input  in_1,
  input  in_2,
  input  in_3,
  input  in_4,
  input  in_5,
  input  in_6,
  input  in_7,
  input  in_8,
  input  in_9,
  input  in_10,
  input  in_11,
  input  in_12,
  input  in_13,
  input  in_14,
  input  in_15,
  input  in_16,
  input  in_17,
  input  in_18,
  input  in_19,
  input  in_20,
  input  in_21,
  input  in_22,
  input  in_23,
  input  in_24,
  input  in_25,
  input  in_26,
  input  in_27,
  input  in_28,
  input  in_29,
  input  in_30,
  input  in_31,
  input  in_32,
  input  in_33,
  input  in_34,
  output [1:0] out_35,
  output [3:0] out_36,
  output out_37,
  output out_38,
  output out_39,
  output out_40,
  output out_41,
  output out_42,
  output [2:0] out_43,
  output [1:0] out_44,
  output [3:0] out_45,
  output [2:0] out_46,
  output [1:0] out_47,
  output [3:0] out_48,
  output [2:0] out_49,
  output [3:0] out_50,
  output [1:0] out_51,
  output [2:0] out_52,
  output [1:0] out_53,
  output [3:0] out_54,
  output [2:0] out_55,
  output [1:0] out_56,
  output [3:0] out_57,
  output [2:0] out_58,
  output [1:0] out_59,
  output [3:0] out_60,
  output [2:0] out_61,
  output [1:0] out_62,
  output [3:0] out_63,
  output [2:0] out_64,
  output [1:0] out_65,
  output [3:0] out_66,
  output [2:0] out_67,
  output [1:0] out_68,
  output [3:0] out_69,
  output [2:0] out_70,
  output [1:0] out_71,
  output [3:0] out_72,
  output [2:0] out_73,
  output [1:0] out_74,
  output [3:0] out_75,
  output [2:0] out_76,
  output [3:0] out_77,
  output [2:0] out_78,
  output [1:0] out_79,
  output [3:0] out_80,
  output [2:0] out_81,
  output [1:0] out_82,
  output [3:0] out_83,
  output [2:0] out_84,
  output [1:0] out_85,
  output [3:0] out_86,
  output [2:0] out_87,
  output [1:0] out_88,
  output [3:0] out_89,
  output [2:0] out_90,
  output [1:0] out_91,
  output [3:0] out_92,
  output [2:0] out_93,
  output [1:0] out_94,
  output [3:0] out_95,
  output [2:0] out_96,
  output [1:0] out_97,
  output [3:0] out_98,
  output [2:0] out_99,
  output [1:0] out_100,
  output [3:0] out_101,
  output [2:0] out_102,
  output [1:0] out_103,
  output [3:0] out_104,
  output [2:0] out_105,
  output [1:0] out_106,
  output [3:0] out_107,
  output [2:0] out_108,
  output [1:0] out_109,
  output [3:0] out_110,
  output [2:0] out_111,
  output [1:0] out_112,
  output [3:0] out_113,
  output [2:0] out_114,
  output [1:0] out_115,
  output [3:0] out_116,
  output [2:0] out_117,
  output [1:0] out_118,
  output [3:0] out_119,
  output [2:0] out_120,
  output [1:0] out_121,
  output [3:0] out_122,
  output [2:0] out_123,
  output [1:0] out_124,
  output [3:0] out_125,
  output [2:0] out_126,
  output [1:0] out_127,
  output [3:0] out_128,
  output [1:0] out_129,
  output [2:0] out_130,
  output [3:0] out_131,
  output [1:0] out_132,
  output [2:0] out_133,
  output [3:0] out_134,
  output [1:0] out_135,
  output [2:0] out_136
);

  wire add, and_1_out, and_2_out, and_3_out, and_4_out, not_1_out, or_2_out, or_3_out, or_4_out, or_5_out,
       or_7_out, or_8_out, or_9_out, or_10_out, or_12_out, or_13_out, or_14_out, or_15_out, or_16_out,
       or_17_out, or_18_out, or_20_out, or_21_out, or_22_out, or_23_out, or_24_out, or_25_out, or_26_out,
       or_27_out, or_28_out, or_29_out, or_32_out, or_33_out, or_34_out, or_35_out, or_36_out, or_37_out,
       or_38_out, or_39_out, or_40_out, or_41_out, or_42_out, or_43_out, or_44_out, or_45_out, or_46_out,
       or_47_out, or_48_out, or_49_out, or_50_out, or_51_out, or_52_out, or_53_out, or_54_out, or_55_out,
       or_56_out, or_57_out;
  wire [3:0] Bsel, MemRW;

  or or_1 (out_37, or_2_out, in_4);
  or or_2 (or_2_out, in_5, or_3_out);
  or or_3 (or_3_out, and_2_out, or_4_out);
  or or_4 (or_4_out, and_3_out, or_5_out);
  or or_5 (or_5_out, and_4_out, and_1_out);
  and and_1 (and_1_out, in_9, in_2);
  and and_2 (and_2_out, in_6, in_1);
  and and_3 (and_3_out, in_7, in_1);
  and and_4 (and_4_out, in_8, not_1_out);
  or or_6 (out_38, or_7_out, in_4);
  or or_7 (or_7_out, in_6, or_8_out);
  or or_8 (or_8_out, in_7, or_9_out);
  or or_9 (or_9_out, in_8, or_10_out);
  not not_1 (not_1_out, in_2);
  buf or_10 (or_10_out, in_9);  // OR_Gate
  or or_11 (out_39, or_12_out, in_4);
  or or_12 (or_12_out, in_5, or_13_out);
  or or_13 (or_13_out, in_6, or_14_out);
  or or_14 (or_14_out, in_7, or_15_out);
  or or_15 (or_15_out, in_8, or_16_out);
  or or_16 (or_16_out, in_9, or_17_out);
  or or_17 (or_17_out, in_11, or_18_out);
  or or_18 (or_18_out, in_12, in_12);
  or or_19 (in_12, in_13, or_20_out);
  or or_20 (or_20_out, in_25, or_21_out);
  or or_21 (or_21_out, in_26, or_22_out);
  or or_22 (or_22_out, in_27, or_23_out);
  or or_23 (or_23_out, in_28, or_24_out);
  or or_24 (or_24_out, in_29, or_25_out);
  or or_25 (or_25_out, in_30, or_26_out);
  or or_26 (or_26_out, in_31, or_27_out);
  or or_27 (or_27_out, in_32, or_28_out);
  or or_28 (or_28_out, in_33, or_29_out);
  buf or_29 (or_29_out, in_34);  // OR_Gate
  buf or_30 (out_40, in_11);  // OR_Gate
  or or_31 (out_41, or_32_out, in_3);
  or or_32 (or_32_out, in_4, or_33_out);
  or or_33 (or_33_out, in_5, or_34_out);
  or or_34 (or_34_out, in_10, or_35_out);
  or or_35 (or_35_out, in_12, or_36_out);
  or or_36 (or_36_out, in_13, or_37_out);
  or or_37 (or_37_out, in_14, or_38_out);
  or or_38 (or_38_out, in_15, or_39_out);
  or or_39 (or_39_out, in_16, or_40_out);
  or or_40 (or_40_out, in_17, or_41_out);
  or or_41 (or_41_out, in_18, or_42_out);
  or or_42 (or_42_out, in_19, or_43_out);
  or or_43 (or_43_out, in_20, or_44_out);
  or or_44 (or_44_out, in_21, or_45_out);
  or or_45 (or_45_out, in_22, or_46_out);
  or or_46 (or_46_out, in_23, or_47_out);
  or or_47 (or_47_out, in_24, or_48_out);
  or or_48 (or_48_out, in_25, or_49_out);
  or or_49 (or_49_out, in_26, or_50_out);
  or or_50 (or_50_out, in_27, or_51_out);
  or or_51 (or_51_out, in_28, or_52_out);
  or or_52 (or_52_out, in_29, or_53_out);
  or or_53 (or_53_out, in_30, or_56_out);
  or or_54 (or_54_out, in_33, or_55_out);
  buf or_55 (or_55_out, in_34);  // OR_Gate
  or or_56 (or_56_out, in_31, or_57_out);
  or or_57 (or_57_out, in_32, or_54_out);
  buf or_58 (out_42, in_6);  // OR_Gate
  Multiplexer #(.width(3), .enable("false")) multiplexer_1 (.in0(3'b001), .in1(3'b000), .out(out_43), .sel(in_3));
  Multiplexer #(.width(3), .enable("false")) multiplexer_2 (.in0(3'b000), .in1(3'b100), .out(out_46), .sel(in_4));
  Multiplexer #(.width(3), .enable("false")) multiplexer_3 (.in0(3'b000), .in1(3'b001), .out(out_49), .sel(in_5));
  Multiplexer #(.width(3), .enable("false")) multiplexer_4 (.in0(3'b000), .in1(3'b011), .out(out_52), .sel(in_6));
  Multiplexer #(.width(3), .enable("false")) multiplexer_5 (.in0(3'b000), .in1(3'b011), .out(out_55), .sel(in_7));
  Multiplexer #(.width(3), .enable("false")) multiplexer_6 (.in0(3'b000), .in1(3'b011), .out(out_58), .sel(in_8));
  Multiplexer #(.width(3), .enable("false")) multiplexer_7 (.in0(3'b000), .in1(3'b011), .out(out_61), .sel(in_9));
  Multiplexer #(.width(3), .enable("false")) multiplexer_8 (.in0(3'b001), .in1(3'b000), .out(out_64), .sel(in_10));
  Multiplexer #(.width(3), .enable("false")) multiplexer_9 (.in0(3'b000), .in1(3'b010), .out(out_67), .sel(in_11));
  Multiplexer #(.width(3), .enable("false")) multiplexer_10 (.in0(3'b000), .in1(3'b001), .out(out_70), .sel(in_12));
  Multiplexer #(.width(3), .enable("false")) multiplexer_11 (.in0(3'b000), .in1(3'b001), .out(out_73), .sel(in_13));
  Multiplexer #(.width(3), .enable("false")) multiplexer_12 (.in0(3'b001), .in1(3'b000), .out(out_76), .sel(in_14));
  Multiplexer #(.width(3), .enable("false")) multiplexer_13 (.in0(3'b001), .in1(3'b000), .out(out_78), .sel(in_15));
  Multiplexer #(.width(3), .enable("false")) multiplexer_14 (.in0(3'b001), .in1(3'b000), .out(out_81), .sel(in_16));
  Multiplexer #(.width(3), .enable("false")) multiplexer_15 (.in0(3'b001), .in1(3'b000), .out(out_84), .sel(in_17));
  Multiplexer #(.width(3), .enable("false")) multiplexer_16 (.in0(3'b001), .in1(3'b000), .out(out_87), .sel(in_18));
  Multiplexer #(.width(3), .enable("false")) multiplexer_17 (.in0(3'b001), .in1(3'b000), .out(out_90), .sel(in_19));
  Multiplexer #(.width(3), .enable("false")) multiplexer_18 (.in0(3'b001), .in1(3'b000), .out(out_93), .sel(in_20));
  Multiplexer #(.width(3), .enable("false")) multiplexer_19 (.in0(3'b001), .in1(3'b000), .out(out_96), .sel(in_21));
  Multiplexer #(.width(3), .enable("false")) multiplexer_20 (.in0(3'b001), .in1(3'b000), .out(out_99), .sel(in_22));
  Multiplexer #(.width(3), .enable("false")) multiplexer_21 (.in0(3'b001), .in1(3'b000), .out(out_102), .sel(in_23));
  Multiplexer #(.width(3), .enable("false")) multiplexer_22 (.in0(3'b001), .in1(3'b000), .out(out_111), .sel(in_26));
  Multiplexer #(.width(3), .enable("false")) multiplexer_23 (.in0(3'b000), .in1(3'b001), .out(out_114), .sel(in_27));
  Multiplexer #(.width(3), .enable("false")) multiplexer_24 (.in0(3'b000), .in1(3'b001), .out(out_117), .sel(in_28));
  Multiplexer #(.width(3), .enable("false")) multiplexer_25 (.in0(3'b000), .in1(3'b001), .out(out_120), .sel(in_29));
  Multiplexer #(.width(3), .enable("false")) multiplexer_26 (.in0(3'b000), .in1(3'b001), .out(out_123), .sel(in_30));
  Multiplexer #(.width(3), .enable("false")) multiplexer_27 (.in0(3'b000), .in1(3'b001), .out(out_126), .sel(in_31));
  Multiplexer #(.width(3), .enable("false")) multiplexer_28 (.in0(3'b000), .in1(3'b001), .out(out_130), .sel(in_32));
  Multiplexer #(.width(3), .enable("false")) multiplexer_29 (.in0(3'b000), .in1(3'b001), .out(out_133), .sel(in_33));
  Multiplexer #(.width(3), .enable("false")) multiplexer_30 (.in0(3'b000), .in1(3'b101), .out(out_136), .sel(in_34));
  Multiplexer #(.width(3), .enable("false")) multiplexer_31 (.in0(3'b001), .in1(3'b000), .out(out_105), .sel(in_24));
  Multiplexer #(.width(3), .enable("false")) multiplexer_32 (.in0(3'b001), .in1(3'b000), .out(out_108), .sel(in_25));
  Multiplexer #(.width(2), .enable("false")) multiplexer_33 (.in0(2'b00), .in1(2'b01), .out(out_35), .sel(in_3));
  Multiplexer #(.width(2), .enable("false")) multiplexer_34 (.in0(2'b01), .in1(2'b00), .out(out_44), .sel(in_4));
  Multiplexer #(.width(2), .enable("false")) multiplexer_35 (.in0(2'b01), .in1(2'b00), .out(out_47), .sel(in_5));
  Multiplexer #(.width(2), .enable("false")) multiplexer_36 (.in0(2'b01), .in1(2'b00), .out(out_51), .sel(in_6));
  Multiplexer #(.width(2), .enable("false")) multiplexer_37 (.in0(2'b01), .in1(2'b00), .out(out_53), .sel(in_7));
  Multiplexer #(.width(2), .enable("false")) multiplexer_38 (.in0(2'b00), .in1(2'b01), .out(out_103), .sel(in_23));
  Multiplexer #(.width(2), .enable("false")) multiplexer_39 (.in0(2'b00), .in1(2'b01), .out(out_106), .sel(in_24));
  Multiplexer #(.width(2), .enable("false")) multiplexer_40 (.in0(2'b00), .in1(2'b10), .out(out_109), .sel(in_25));
  Multiplexer #(.width(2), .enable("false")) multiplexer_41 (.in0(2'b00), .in1(2'b10), .out(out_112), .sel(in_26));
  Multiplexer #(.width(2), .enable("false")) multiplexer_42 (.in0(2'b00), .in1(2'b01), .out(out_115), .sel(in_27));
  Multiplexer #(.width(2), .enable("false")) multiplexer_43 (.in0(2'b00), .in1(2'b01), .out(out_118), .sel(in_28));
  Multiplexer #(.width(2), .enable("false")) multiplexer_44 (.in0(2'b00), .in1(2'b01), .out(out_121), .sel(in_29));
  Multiplexer #(.width(2), .enable("false")) multiplexer_45 (.in0(2'b00), .in1(2'b01), .out(out_124), .sel(in_30));
  Multiplexer #(.width(2), .enable("false")) multiplexer_46 (.in0(2'b00), .in1(2'b01), .out(out_127), .sel(in_31));
  Multiplexer #(.width(2), .enable("false")) multiplexer_47 (.in0(2'b00), .in1(2'b01), .out(out_129), .sel(in_32));
  Multiplexer #(.width(2), .enable("false")) multiplexer_48 (.in0(2'b00), .in1(2'b01), .out(out_132), .sel(in_33));
  Multiplexer #(.width(2), .enable("false")) multiplexer_49 (.in0(2'b00), .in1(2'b01), .out(out_135), .sel(in_34));
  Multiplexer #(.width(2), .enable("false")) multiplexer_50 (.in0(2'b01), .in1(2'b00), .out(out_56), .sel(in_8));
  Multiplexer #(.width(2), .enable("false")) multiplexer_51 (.in0(2'b01), .in1(2'b00), .out(out_59), .sel(in_9));
  Multiplexer #(.width(2), .enable("false")) multiplexer_52 (.in0(2'b00), .in1(2'b01), .out(out_62), .sel(in_10));
  Multiplexer #(.width(2), .enable("false")) multiplexer_53 (.in0(2'b01), .in1(2'b00), .out(out_65), .sel(in_11));
  Multiplexer #(.width(2), .enable("false")) multiplexer_54 (.in0(2'b00), .in1(2'b10), .out(out_68), .sel(in_12));
  Multiplexer #(.width(2), .enable("false")) multiplexer_55 (.in0(2'b00), .in1(2'b01), .out(out_71), .sel(in_13));
  Multiplexer #(.width(2), .enable("false")) multiplexer_56 (.in0(2'b00), .in1(2'b01), .out(out_74), .sel(in_14));
  Multiplexer #(.width(2), .enable("false")) multiplexer_57 (.in0(2'b00), .in1(2'b01), .out(out_79), .sel(in_15));
  Multiplexer #(.width(2), .enable("false")) multiplexer_58 (.in0(2'b00), .in1(2'b01), .out(out_82), .sel(in_16));
  Multiplexer #(.width(2), .enable("false")) multiplexer_59 (.in0(2'b00), .in1(2'b01), .out(out_85), .sel(in_17));
  Multiplexer #(.width(2), .enable("false")) multiplexer_60 (.in0(2'b00), .in1(2'b01), .out(out_88), .sel(in_18));
  Multiplexer #(.width(2), .enable("false")) multiplexer_61 (.in0(2'b00), .in1(2'b01), .out(out_91), .sel(in_19));
  Multiplexer #(.width(2), .enable("false")) multiplexer_62 (.in0(2'b00), .in1(2'b01), .out(out_94), .sel(in_20));
  Multiplexer #(.width(2), .enable("false")) multiplexer_63 (.in0(2'b00), .in1(2'b01), .out(out_97), .sel(in_21));
  Multiplexer #(.width(2), .enable("false")) multiplexer_64 (.in0(2'b00), .in1(2'b01), .out(out_100), .sel(in_22));
  Multiplexer #(.width(4), .enable("false")) multiplexer_65 (.in0(4'b0001), .in1(4'b0000), .out(MemRW), .sel(add));
  Multiplexer #(.width(4), .enable("false")) multiplexer_66 (.in0(4'b0001), .in1(4'b0000), .out(Bsel), .sel(add));
  Multiplexer #(.width(4), .enable("false")) multiplexer_67 (.in0(4'b0001), .in1(4'b0000), .out(out_36), .sel(in_3));
  Multiplexer #(.width(4), .enable("false")) multiplexer_68 (.in0(4'b0001), .in1(4'b0000), .out(out_45), .sel(in_4));
  Multiplexer #(.width(4), .enable("false")) multiplexer_69 (.in0(4'b0001), .in1(4'b0000), .out(out_48), .sel(in_5));
  Multiplexer #(.width(4), .enable("false")) multiplexer_70 (.in0(4'b0001), .in1(4'b0000), .out(out_50), .sel(in_6));
  Multiplexer #(.width(4), .enable("false")) multiplexer_71 (.in0(4'b0001), .in1(4'b0000), .out(out_54), .sel(in_7));
  Multiplexer #(.width(4), .enable("false")) multiplexer_72 (.in0(4'b0001), .in1(4'b0000), .out(out_57), .sel(in_8));
  Multiplexer #(.width(4), .enable("false")) multiplexer_73 (.in0(4'b0001), .in1(4'b0000), .out(out_60), .sel(in_9));
  Multiplexer #(.width(4), .enable("false")) multiplexer_74 (.in0(4'b0001), .in1(4'b1100), .out(out_63), .sel(in_10));
  Multiplexer #(.width(4), .enable("false")) multiplexer_75 (.in0(4'b0001), .in1(4'b0000), .out(out_66), .sel(in_11));
  Multiplexer #(.width(4), .enable("false")) multiplexer_76 (.in0(4'b0001), .in1(4'b0000), .out(out_69), .sel(in_12));
  Multiplexer #(.width(4), .enable("false")) multiplexer_77 (.in0(4'b0001), .in1(4'b0000), .out(out_72), .sel(in_13));
  Multiplexer #(.width(4), .enable("false")) multiplexer_78 (.in0(4'b0001), .in1(4'b1010), .out(out_75), .sel(in_14));
  Multiplexer #(.width(4), .enable("false")) multiplexer_79 (.in0(4'b0001), .in1(4'b0110), .out(out_77), .sel(in_15));
  Multiplexer #(.width(4), .enable("false")) multiplexer_80 (.in0(4'b0001), .in1(4'b1010), .out(out_80), .sel(in_16));
  Multiplexer #(.width(4), .enable("false")) multiplexer_81 (.in0(4'b0001), .in1(4'b1011), .out(out_83), .sel(in_17));
  Multiplexer #(.width(4), .enable("false")) multiplexer_82 (.in0(4'b0001), .in1(4'b0111), .out(out_86), .sel(in_18));
  Multiplexer #(.width(4), .enable("false")) multiplexer_83 (.in0(4'b0001), .in1(4'b0011), .out(out_89), .sel(in_19));
  Multiplexer #(.width(4), .enable("false")) multiplexer_84 (.in0(4'b0001), .in1(4'b1000), .out(out_92), .sel(in_20));
  Multiplexer #(.width(4), .enable("false")) multiplexer_85 (.in0(4'b0001), .in1(4'b0100), .out(out_95), .sel(in_21));
  Multiplexer #(.width(4), .enable("false")) multiplexer_86 (.in0(4'b0001), .in1(4'b0010), .out(out_98), .sel(in_22));
  Multiplexer #(.width(4), .enable("false")) multiplexer_87 (.in0(4'b0001), .in1(4'b1001), .out(out_101), .sel(in_23));
  Multiplexer #(.width(4), .enable("false")) multiplexer_88 (.in0(4'b0000), .in1(4'b0001), .out(out_104), .sel(in_24));
  Multiplexer #(.width(4), .enable("false")) multiplexer_89 (.in0(4'b0001), .in1(4'b0000), .out(out_107), .sel(in_25));
  Multiplexer #(.width(4), .enable("false")) multiplexer_90 (.in0(4'b0001), .in1(4'b0000), .out(out_110), .sel(in_26));
  Multiplexer #(.width(4), .enable("false")) multiplexer_91 (.in0(4'b0001), .in1(4'b0110), .out(out_113), .sel(in_27));
  Multiplexer #(.width(4), .enable("false")) multiplexer_92 (.in0(4'b0001), .in1(4'b0111), .out(out_116), .sel(in_28));
  Multiplexer #(.width(4), .enable("false")) multiplexer_93 (.in0(4'b0001), .in1(4'b0011), .out(out_119), .sel(in_29));
  Multiplexer #(.width(4), .enable("false")) multiplexer_94 (.in0(4'b0001), .in1(4'b0100), .out(out_122), .sel(in_30));
  Multiplexer #(.width(4), .enable("false")) multiplexer_95 (.in0(4'b0001), .in1(4'b0101), .out(out_125), .sel(in_31));
  Multiplexer #(.width(4), .enable("false")) multiplexer_96 (.in0(4'b0001), .in1(4'b0010), .out(out_128), .sel(in_32));
  Multiplexer #(.width(4), .enable("false")) multiplexer_97 (.in0(4'b0000), .in1(4'b0001), .out(out_131), .sel(in_33));
  Multiplexer #(.width(4), .enable("false")) multiplexer_98 (.in0(4'b0001), .in1(4'b1101), .out(out_134), .sel(in_34));
  // Pins of 1 and 4 bits meet at MemRW
  // Pins of 1 and 4 bits meet at Bsel

  // Notes on the sheet:
  //   IN THIS FILE WE USE CONTROL LOGIC TO DETERMINE IF EACH OF OUR INSTRUCTIONS HAS PCSEL, REGWEN, ETC 1 or 0.
endmodule
