// Logisim project regfile.circ as structural Verilog: 10 circuits, main circuit main
module main (
  input  [4:0] rs1,
  input  [4:0] rs2,
  input  [4:0] rd,
  input  [31:0] Write_Data,
  input  RegWEn,
  input  clk,
  output [31:0] ra,
  output [31:0] sp,
  output [31:0] t0,
  output [31:0] t1,
  output [31:0] t2,
  output [31:0] s0,
  output [31:0] s1,
  output [31:0] a0,
  output [31:0] Read_Data_1,
  output [31:0] Read_Data_2
);

  wire comparator_1_eq, comparator_2_eq, comparator_3_eq, comparator_4_eq, comparator_5_eq, comparator_6_eq,
       comparator_7_eq, comparator_8_eq;
  wire [31:0] multiplexer_1_out, multiplexer_2_out, multiplexer_3_out, multiplexer_4_out, multiplexer_5_out,
       multiplexer_6_out, multiplexer_8_out, multiplexer_9_out, zero_in, zero_q;

  Register #(.width(32)) zero (.D(zero_in), .en(1'b0), .clk(clk), .Q(zero_q));  // open: clr
  Comparator #(.width(5), .mode("unsigned")) comparator_1 (.a(rd), .b(5'b01001), .eq(comparator_1_eq));  // open: gt, lt
  Comparator #(.width(5), .mode("unsigned")) comparator_2 (.a(rd), .b(5'b01010), .eq(comparator_2_eq));  // open: gt, lt
  Register #(.width(32)) x9 (.D(multiplexer_1_out), .en(RegWEn), .clk(clk), .Q(s1));  // open: clr
  Multiplexer #(.width(32), .enable("false")) multiplexer_1 (
    .in0(s1), .in1(Write_Data), .out(multiplexer_1_out), .sel(comparator_1_eq));
  Register #(.width(32)) x10 (.D(multiplexer_2_out), .en(RegWEn), .clk(clk), .Q(a0));  // open: clr
  Multiplexer #(.width(32), .enable("false")) multiplexer_2 (
    .in0(a0), .in1(Write_Data), .out(multiplexer_2_out), .sel(comparator_2_eq));
  Comparator #(.width(5), .mode("unsigned")) comparator_3 (.a(rd), .b(5'b00001), .eq(comparator_3_eq));  // open: gt, lt
  Comparator #(.width(5), .mode("unsigned")) comparator_4 (.a(rd), .b(5'b00010), .eq(comparator_4_eq));  // open: gt, lt
  Multiplexer #(.width(32), .enable("false")) multiplexer_3 (
    .in0(sp), .in1(Write_Data), .out(multiplexer_3_out), .sel(comparator_4_eq));
  Comparator #(.width(5), .mode("unsigned")) comparator_5 (.a(rd), .b(5'b00101), .eq(comparator_5_eq));  // open: gt, lt
  Comparator #(.width(5), .mode("unsigned")) comparator_6 (.a(rd), .b(5'b00110), .eq(comparator_6_eq));  // open: gt, lt
  Multiplexer #(.width(32), .enable("false")) multiplexer_4 (
    .in0(ra), .in1(Write_Data), .out(multiplexer_4_out), .sel(comparator_3_eq));
  Register #(.width(32)) x1 (.D(multiplexer_4_out), .en(RegWEn), .clk(clk), .Q(ra));  // open: clr
  Register #(.width(32)) x2 (.D(multiplexer_3_out), .en(RegWEn), .clk(clk), .Q(sp));  // open: clr
  Multiplexer #(.width(32), .enable("false")) multiplexer_5 (
    .in0(t0), .in1(Write_Data), .out(multiplexer_5_out), .sel(comparator_5_eq));
  Multiplexer #(.width(32), .enable("false")) multiplexer_6 (
    .in0(t1), .in1(Write_Data), .out(multiplexer_6_out), .sel(comparator_6_eq));
  Register #(.width(32)) x5 (.D(multiplexer_5_out), .en(RegWEn), .clk(clk), .Q(t0));  // open: clr
  Register #(.width(32)) x6 (.D(multiplexer_6_out), .en(RegWEn), .clk(clk), .Q(t1));  // open: clr
  Comparator #(.width(5), .mode("unsigned")) comparator_7 (.a(rd), .b(5'b00111), .eq(comparator_7_eq));  // open: gt, lt
  Multiplexer #(.select(5), .width(32), .enable("false")) multiplexer_7 (
    .in0({32{1'b0}}), .in1(ra), .in2(sp), .in3({32{1'b0}}), .in4({32{1'b0}}), .in5(t0), .in6(t1), .in7(t2),
    .in8(s0), .in9(s1), .in10(a0), .in11({32{1'b0}}), .in12({32{1'b0}}), .in13({32{1'b0}}),
    .in14({32{1'b0}}), .in15({32{1'b0}}), .in16({32{1'b0}}), .in17({32{1'b0}}), .in18({32{1'b0}}),
    .in19({32{1'b0}}), .in20({32{1'b0}}), .in21({32{1'b0}}), .in22({32{1'b0}}), .in23({32{1'b0}}),
    .in24({32{1'b0}}), .in25({32{1'b0}}), .in26({32{1'b0}}), .in27({32{1'b0}}), .in28({32{1'b0}}),
    .in29({32{1'b0}}), .in30({32{1'b0}}), .in31({32{1'b0}}), .out(Read_Data_1), .sel(rs1));
  Register #(.width(32)) x7 (.D(multiplexer_8_out), .en(RegWEn), .clk(clk), .Q(t2));  // open: clr
  Multiplexer #(.width(32), .enable("false")) multiplexer_8 (
    .in0(t2), .in1(Write_Data), .out(multiplexer_8_out), .sel(comparator_7_eq));
  Comparator #(.width(5), .mode("unsigned")) comparator_8 (.a(rd), .b(5'b01000), .eq(comparator_8_eq));  // open: gt, lt
  Register #(.width(32)) x8 (.D(multiplexer_9_out), .en(RegWEn), .clk(clk), .Q(s0));  // open: clr
  Multiplexer #(.width(32), .enable("false")) multiplexer_9 (
    .in0(s0), .in1(Write_Data), .out(multiplexer_9_out), .sel(comparator_8_eq));
  Multiplexer #(.select(5), .width(32), .enable("false")) multiplexer_10 (
    .in0({32{1'b0}}), .in1(ra), .in2(sp), .in3({32{1'b0}}), .in4({32{1'b0}}), .in5(t0), .in6(t1), .in7(t2),
    .in8(s0), .in9(s1), .in10(a0), .in11({32{1'b0}}), .in12({32{1'b0}}), .in13({32{1'b0}}),
    .in14({32{1'b0}}), .in15({32{1'b0}}), .in16({32{1'b0}}), .in17({32{1'b0}}), .in18({32{1'b0}}),
    .in19({32{1'b0}}), .in20({32{1'b0}}), .in21({32{1'b0}}), .in22({32{1'b0}}), .in23({32{1'b0}}),
    .in24({32{1'b0}}), .in25({32{1'b0}}), .in26({32{1'b0}}), .in27({32{1'b0}}), .in28({32{1'b0}}),
    .in29({32{1'b0}}), .in30({32{1'b0}}), .in31({32{1'b0}}), .out(Read_Data_2), .sel(rs2));
  // also tied to GND on the sheet: {zero_q[0], zero_q[1], zero_q[2], zero_q[3], zero_q[4], zero_q[5], zero_q[6], zero_q[7], zero_q[8], zero_q[9], zero_q[10], zero_q[11], zero_q[12], zero_q[13], zero_q[14], zero_q[15], zero_q[16], zero_q[17], zero_q[18], zero_q[19], zero_q[20], zero_q[21], zero_q[22], zero_q[23], zero_q[24], zero_q[25], zero_q[26], zero_q[27], zero_q[28], zero_q[29], zero_q[30], zero_q[31]}

  // Other names for the same wires on the sheet: read_data1[31:0] = Read_Data_1; read_data2[31:0] = Read_Data_2;
  //   read_reg1[4:0] = rs1; read_reg2[4:0] = rs2; write_en = RegWEn; write_reg[4:0] = rd

  // Notes on the sheet:
  //   INPUTS to your circuit
  //   DON'T CHANGE THE LOCATIONS OF THE INPUTS AND OUTPUTS!
  //   These are DEBUG/TEST outputs from your circuit.
  //   OUTPUTS from your circuit
endmodule

module x0 (
  input  [31:0] zero_in,
  input  write_en,
  input  clk
);

  wire [31:0] zero_q;

  Register #(.width(32)) zero (.D(zero_in), .en(write_en), .clk(clk), .Q(zero_q));  // open: clr
  // also tied to GND on the sheet: {zero_q[0], zero_q[1], zero_q[2], zero_q[3], zero_q[4], zero_q[5], zero_q[6], zero_q[7], zero_q[8], zero_q[9], zero_q[10], zero_q[11], zero_q[12], zero_q[13], zero_q[14], zero_q[15], zero_q[16], zero_q[17], zero_q[18], zero_q[19], zero_q[20], zero_q[21], zero_q[22], zero_q[23], zero_q[24], zero_q[25], zero_q[26], zero_q[27], zero_q[28], zero_q[29], zero_q[30], zero_q[31]}

  // Notes on the sheet:
  //   clk: pull=down
endmodule

module x1 (
  input  [31:0] ra_in,
  input  write_en,
  input  clk,
  output [31:0] ra_out
);

  Register #(.width(32)) ra (.D(ra_in), .en(write_en), .clk(clk), .Q(ra_out));  // open: clr

  // Notes on the sheet:
  //   clk: pull=down
endmodule

module x2 (
  input  [31:0] sp_in,
  input  write_en,
  input  clk,
  output [31:0] sp_out
);

  Register #(.width(32)) sp (.D(sp_in), .en(write_en), .clk(clk), .Q(sp_out));  // open: clr

  // Notes on the sheet:
  //   clk: pull=down
endmodule

module x5 (
  input  [31:0] t0_in,
  input  write_en,
  input  clk,
  output [31:0] t0_out
);

  Register #(.width(32)) t0 (.D(t0_in), .en(write_en), .clk(clk), .Q(t0_out));  // open: clr

  // Notes on the sheet:
  //   clk: pull=down
endmodule

module x6 (
  input  [31:0] t1_in,
  input  write_en,
  input  clk,
  output [31:0] t1_out
);

  Register #(.width(32)) t1 (.D(t1_in), .en(write_en), .clk(clk), .Q(t1_out));  // open: clr

  // Notes on the sheet:
  //   clk: pull=down
endmodule

module x7 (
  input  [31:0] t2_in,
  input  write_en,
  input  clk,
  output [31:0] t2_out
);

  Register #(.width(32)) t2 (.D(t2_in), .en(write_en), .clk(clk), .Q(t2_out));  // open: clr

  // Notes on the sheet:
  //   clk: pull=down
endmodule

module x8 (
  input  [31:0] s0_in,
  input  write_en,
  input  clk,
  output [31:0] s0_out
);

  Register #(.width(32)) s0 (.D(s0_in), .en(write_en), .clk(clk), .Q(s0_out));  // open: clr

  // Notes on the sheet:
  //   clk: pull=down
endmodule

module x9 (
  input  [31:0] s1_in,
  input  write_en,
  input  clk,
  output [31:0] s1_out
);

  Register #(.width(32)) s1 (.D(s1_in), .en(write_en), .clk(clk), .Q(s1_out));  // open: clr

  // Notes on the sheet:
  //   clk: pull=down
endmodule

module x10 (
  input  [31:0] a0_in,
  input  write_en,
  input  clk,
  output [31:0] a0_out
);

  Register #(.width(32)) a0 (.D(a0_in), .en(write_en), .clk(clk), .Q(a0_out));  // open: clr

  // Notes on the sheet:
  //   clk: pull=down
endmodule
